// Digital circuit 74FFWithForceLoad.dig as structural Verilog
module _74FFWithForceLoad (
  input  CLK,
  input  D,
  input  Load_A,
  input  Load_B,
  input  CLR,
  input  PRE,
  output Always,
  output Loaded_A,
  output Loaded_B
);

  wire nand_1_out, nand_2_out, nand_3_out, nand_4_out, nand_6_out, not_1_out, not_2_out;

  not not_1 (not_1_out, PRE);
  PullDown pulldown_1 (.out(PRE));
  not not_2 (not_2_out, CLR);
  PullDown pulldown_2 (.out(D));
  nand nand_1 (nand_1_out, not_1_out, nand_4_out, nand_2_out);
  nand nand_2 (nand_2_out, nand_1_out, not_2_out, CLK);
  nand nand_3 (nand_3_out, nand_2_out, CLK, nand_4_out);
  nand nand_4 (nand_4_out, nand_3_out, not_2_out, D);
  nand nand_5 (Always, not_1_out, nand_2_out, nand_6_out);
  nand nand_6 (nand_6_out, Always, not_2_out, nand_3_out);
  assign Loaded_A = Load_A ? Always : 1'bz;  // Driver driver_1
  assign Loaded_B = Load_B ? Always : 1'bz;  // Driver driver_2

  // Notes on the sheet:
  //   Edge Flop
  //   Latch
endmodule

/* Test case:
# Test Case for Tri-state Gated Register
CLK Data Reset Load_A Load_B Always Loaded_A Loaded_B

# 1. Init: Reset the register
0   0    1     0      0      0      Z        Z
C   0    1     0      0      0      Z        Z
0   0    0     0      0      0      Z        Z

# 2. Store a '1' on rising edge
# Always should update, but Loaded A/B remain disconnected
C   1    0     0      0      1      Z        Z

# 3. Test Tri-state Gate A
0   1    0     1      0      1      1        Z
0   1    0     0      0      1      Z        Z

# 4. Test Tri-state Gate B
0   1    0     0      1      1      Z        1
0   1    0     0      0      1      Z        Z

# 5. Stability Test: Change data while CLK is LOW
# Value must stay 1, and gates must follow Load pins
0   0    0     1      1      1      1        1
0   0    0     0      0      1      Z        Z

# 6. Stability Test: Change data while CLK is HIGH
# (Crucial for 3-latch designs to check for 'bleed-through')
1   0    0     1      1      1      1        1
1   0    0     0      0      1      Z        Z

# 7. Overwrite with '0'
C   0    0     1      1      0      0        0

# 8. Reset Test while data is 1
C   1    0     0      0      1      Z        Z
0   1    1     1      1      0      0        0
*/
