// Digital circuit ALUnoCLA.dig as structural Verilog
module ALUnoCLA (
  input  C_0,
  input  C_1,
  input  C_2,
  input  [7:0] A_0,
  input  [7:0] B_0,
  output [7:0] C_Arith
);

  wire and_7_out, and_8_out, and_9_out, and_10_out, and_11_out, and_12_out, and_13_out, and_14_out,
       and_17_out, and_18_out, and_19_out, and_20_out, and_21_out, and_22_out, and_23_out, and_24_out,
       and_25_out, and_26_out, and_27_out, and_28_out, and_29_out, and_30_out, and_31_out, and_32_out,
       and_33_out, and_34_out, and_35_out, and_36_out, and_37_out, and_38_out, and_39_out, not_1_out,
       not_2_out, not_3_out, not_4_out, not_5_out, not_6_out, not_7_out, or_8_out, or_9_out, or_10_out,
       or_11_out, or_12_out, or_13_out, or_14_out, or_15_out, or_17_out, xor_1_out, xor_2_out, xor_3_out,
       xor_4_out, xor_5_out, xor_6_out, xor_7_out, xor_8_out, xor_15_out, xor_16_out, xor_17_out, xor_18_out,
       xor_19_out, xor_20_out, xor_21_out, xor_22_out;
  wire [7:0] and_16_out, nand_8_out, nor_8_out, or_16_out, xor_24_out, xor_32_out;

  xor xor_1 (xor_1_out, B_0[7], and_34_out);
  xor xor_2 (xor_2_out, B_0[6], and_34_out);
  xor xor_3 (xor_3_out, B_0[5], and_34_out);
  xor xor_4 (xor_4_out, B_0[4], and_34_out);
  xor xor_5 (xor_5_out, B_0[3], and_34_out);
  xor xor_6 (xor_6_out, B_0[2], and_34_out);
  xor xor_7 (xor_7_out, B_0[1], and_34_out);
  xor xor_8 (xor_8_out, B_0[0], and_34_out);
  and and_1 (and_16_out[0], B_0[0], A_0[0]);
  and and_2 (and_16_out[1], B_0[1], A_0[1]);
  nand nand_1 (nand_8_out[0], B_0[0], A_0[0]);
  nand nand_2 (nand_8_out[1], B_0[1], A_0[1]);
  or or_1 (or_16_out[0], B_0[0], A_0[0]);
  or or_2 (or_16_out[1], B_0[1], A_0[1]);
  nor nor_1 (nor_8_out[0], B_0[0], A_0[0]);
  nor nor_2 (nor_8_out[1], B_0[1], A_0[1]);
  xor xor_9 (xor_24_out[0], B_0[0], A_0[0]);
  xor xor_10 (xor_24_out[1], B_0[1], A_0[1]);
  and and_3 (and_16_out[2], B_0[2], A_0[2]);
  nand nand_3 (nand_8_out[2], B_0[2], A_0[2]);
  or or_3 (or_16_out[2], B_0[2], A_0[2]);
  nor nor_3 (nor_8_out[2], B_0[2], A_0[2]);
  xor xor_11 (xor_24_out[2], B_0[2], A_0[2]);
  and and_4 (and_16_out[3], B_0[3], A_0[3]);
  nand nand_4 (nand_8_out[3], B_0[3], A_0[3]);
  or or_4 (or_16_out[3], B_0[3], A_0[3]);
  nor nor_4 (nor_8_out[3], B_0[3], A_0[3]);
  xor xor_12 (xor_24_out[3], B_0[3], A_0[3]);
  and and_5 (and_16_out[4], B_0[4], A_0[4]);
  and and_6 (and_16_out[5], B_0[5], A_0[5]);
  nand nand_5 (nand_8_out[4], B_0[4], A_0[4]);
  nand nand_6 (nand_8_out[5], B_0[5], A_0[5]);
  or or_5 (or_16_out[4], B_0[4], A_0[4]);
  or or_6 (or_16_out[5], B_0[5], A_0[5]);
  nor nor_5 (nor_8_out[4], B_0[4], A_0[4]);
  nor nor_6 (nor_8_out[5], B_0[5], A_0[5]);
  xor xor_13 (xor_24_out[4], B_0[4], A_0[4]);
  xor xor_14 (xor_24_out[5], B_0[5], A_0[5]);
  and and_7 (and_7_out, xor_1_out, A_0[7]);
  xor xor_15 (xor_15_out, A_0[7], xor_1_out);
  and and_8 (and_8_out, xor_2_out, A_0[6]);
  xor xor_16 (xor_16_out, A_0[6], xor_2_out);
  and and_9 (and_9_out, xor_3_out, A_0[5]);
  xor xor_17 (xor_17_out, A_0[5], xor_3_out);
  and and_10 (and_10_out, xor_4_out, A_0[4]);
  xor xor_18 (xor_18_out, A_0[4], xor_4_out);
  and and_11 (and_11_out, xor_5_out, A_0[3]);
  xor xor_19 (xor_19_out, A_0[3], xor_5_out);
  and and_12 (and_12_out, xor_6_out, A_0[2]);
  xor xor_20 (xor_20_out, A_0[2], xor_6_out);
  and and_13 (and_13_out, xor_7_out, A_0[1]);
  xor xor_21 (xor_21_out, A_0[1], xor_7_out);
  and and_14 (and_14_out, xor_8_out, A_0[0]);
  xor xor_22 (xor_22_out, A_0[0], xor_8_out);
  and and_15 (and_16_out[6], B_0[6], A_0[6]);
  nand nand_7 (nand_8_out[6], B_0[6], A_0[6]);
  or or_7 (or_16_out[6], B_0[6], A_0[6]);
  nor nor_7 (nor_8_out[6], B_0[6], A_0[6]);
  xor xor_23 (xor_24_out[6], B_0[6], A_0[6]);
  or or_8 (or_8_out, and_7_out, and_17_out);
  or or_9 (or_9_out, and_8_out, and_18_out);
  or or_10 (or_10_out, and_9_out, and_19_out);
  or or_11 (or_11_out, and_10_out, and_20_out);
  or or_12 (or_12_out, and_11_out, and_21_out);
  or or_13 (or_13_out, and_12_out, and_22_out);
  or or_14 (or_14_out, and_13_out, and_23_out);
  or or_15 (or_15_out, and_14_out, and_24_out);
  and and_16 (and_16_out[7], B_0[7], A_0[7]);
  nand nand_8 (nand_8_out[7], B_0[7], A_0[7]);
  or or_16 (or_16_out[7], B_0[7], A_0[7]);
  nor nor_8 (nor_8_out[7], B_0[7], A_0[7]);
  xor xor_24 (xor_24_out[7], B_0[7], A_0[7]);
  and and_17 (and_17_out, xor_15_out, or_9_out);
  xor xor_25 (xor_32_out[7], xor_15_out, or_9_out);
  and and_18 (and_18_out, xor_16_out, or_10_out);
  xor xor_26 (xor_32_out[6], xor_16_out, or_10_out);
  and and_19 (and_19_out, xor_17_out, or_11_out);
  xor xor_27 (xor_32_out[5], xor_17_out, or_11_out);
  and and_20 (and_20_out, xor_18_out, or_12_out);
  xor xor_28 (xor_32_out[4], xor_18_out, or_12_out);
  and and_21 (and_21_out, xor_19_out, or_13_out);
  xor xor_29 (xor_32_out[3], xor_19_out, or_13_out);
  and and_22 (and_22_out, xor_20_out, or_14_out);
  xor xor_30 (xor_32_out[2], xor_20_out, or_14_out);
  and and_23 (and_23_out, xor_21_out, or_15_out);
  xor xor_31 (xor_32_out[1], xor_21_out, or_15_out);
  and and_24 (and_24_out, xor_22_out, and_34_out);
  xor xor_32 (xor_32_out[0], xor_22_out, and_34_out);
  assign C_Arith[0] = and_35_out ? and_16_out[0] : 1'bz;  // Driver driver_1
  assign C_Arith[1] = and_35_out ? and_16_out[1] : 1'bz;  // Driver driver_2
  assign C_Arith[0] = and_36_out ? nand_8_out[0] : 1'bz;  // Driver driver_3
  assign C_Arith[1] = and_36_out ? nand_8_out[1] : 1'bz;  // Driver driver_4
  assign C_Arith[0] = and_37_out ? or_16_out[0] : 1'bz;  // Driver driver_5
  assign C_Arith[1] = and_37_out ? or_16_out[1] : 1'bz;  // Driver driver_6
  assign C_Arith[0] = and_38_out ? nor_8_out[0] : 1'bz;  // Driver driver_7
  assign C_Arith[1] = and_38_out ? nor_8_out[1] : 1'bz;  // Driver driver_8
  assign C_Arith[0] = and_39_out ? xor_24_out[0] : 1'bz;  // Driver driver_9
  assign C_Arith[1] = and_39_out ? xor_24_out[1] : 1'bz;  // Driver driver_10
  assign C_Arith[2] = and_35_out ? and_16_out[2] : 1'bz;  // Driver driver_11
  assign C_Arith[3] = and_35_out ? and_16_out[3] : 1'bz;  // Driver driver_12
  assign C_Arith[2] = and_36_out ? nand_8_out[2] : 1'bz;  // Driver driver_13
  assign C_Arith[3] = and_36_out ? nand_8_out[3] : 1'bz;  // Driver driver_14
  assign C_Arith[2] = and_37_out ? or_16_out[2] : 1'bz;  // Driver driver_15
  assign C_Arith[3] = and_37_out ? or_16_out[3] : 1'bz;  // Driver driver_16
  assign C_Arith[2] = and_38_out ? nor_8_out[2] : 1'bz;  // Driver driver_17
  assign C_Arith[3] = and_38_out ? nor_8_out[3] : 1'bz;  // Driver driver_18
  assign C_Arith[2] = and_39_out ? xor_24_out[2] : 1'bz;  // Driver driver_19
  assign C_Arith[3] = and_39_out ? xor_24_out[3] : 1'bz;  // Driver driver_20
  assign C_Arith[4] = and_35_out ? and_16_out[4] : 1'bz;  // Driver driver_21
  assign C_Arith[5] = and_35_out ? and_16_out[5] : 1'bz;  // Driver driver_22
  assign C_Arith[4] = and_36_out ? nand_8_out[4] : 1'bz;  // Driver driver_23
  assign C_Arith[5] = and_36_out ? nand_8_out[5] : 1'bz;  // Driver driver_24
  assign C_Arith[4] = and_37_out ? or_16_out[4] : 1'bz;  // Driver driver_25
  assign C_Arith[5] = and_37_out ? or_16_out[5] : 1'bz;  // Driver driver_26
  assign C_Arith[4] = and_38_out ? nor_8_out[4] : 1'bz;  // Driver driver_27
  assign C_Arith[5] = and_38_out ? nor_8_out[5] : 1'bz;  // Driver driver_28
  assign C_Arith[4] = and_39_out ? xor_24_out[4] : 1'bz;  // Driver driver_29
  assign C_Arith[5] = and_39_out ? xor_24_out[5] : 1'bz;  // Driver driver_30
  assign C_Arith[6] = and_35_out ? and_16_out[6] : 1'bz;  // Driver driver_31
  assign C_Arith[7] = and_35_out ? and_16_out[7] : 1'bz;  // Driver driver_32
  assign C_Arith[6] = and_36_out ? nand_8_out[6] : 1'bz;  // Driver driver_33
  assign C_Arith[7] = and_36_out ? nand_8_out[7] : 1'bz;  // Driver driver_34
  assign C_Arith[6] = and_37_out ? or_16_out[6] : 1'bz;  // Driver driver_35
  assign C_Arith[7] = and_37_out ? or_16_out[7] : 1'bz;  // Driver driver_36
  assign C_Arith[6] = and_38_out ? nor_8_out[6] : 1'bz;  // Driver driver_37
  assign C_Arith[7] = and_38_out ? nor_8_out[7] : 1'bz;  // Driver driver_38
  assign C_Arith[6] = and_39_out ? xor_24_out[6] : 1'bz;  // Driver driver_39
  assign C_Arith[7] = and_39_out ? xor_24_out[7] : 1'bz;  // Driver driver_40
  not not_1 (not_1_out, C_2);
  assign C_Arith[0] = or_17_out ? xor_32_out[0] : 1'bz;  // Driver driver_41
  not not_2 (not_2_out, C_1);
  not not_3 (not_3_out, C_1);
  assign C_Arith[1] = or_17_out ? xor_32_out[1] : 1'bz;  // Driver driver_42
  assign C_Arith[2] = or_17_out ? xor_32_out[2] : 1'bz;  // Driver driver_43
  not not_4 (not_4_out, C_0);
  and and_25 (and_25_out, not_4_out, not_2_out);
  and and_26 (and_26_out, C_0, not_2_out);
  and and_27 (and_27_out, not_4_out, C_1);
  and and_28 (and_28_out, C_1, C_0);
  not not_5 (not_5_out, C_2);
  not not_6 (not_6_out, C_0);
  and and_29 (and_29_out, not_6_out, not_3_out);
  and and_30 (and_30_out, C_0, not_3_out);
  and and_31 (and_31_out, not_6_out, C_1);
  and and_32 (and_32_out, C_1, C_0);
  not not_7 (not_7_out, not_1_out);
  assign C_Arith[3] = or_17_out ? xor_32_out[3] : 1'bz;  // Driver driver_44
  assign C_Arith[4] = or_17_out ? xor_32_out[4] : 1'bz;  // Driver driver_45
  assign C_Arith[5] = or_17_out ? xor_32_out[5] : 1'bz;  // Driver driver_46
  assign C_Arith[6] = or_17_out ? xor_32_out[6] : 1'bz;  // Driver driver_47
  and and_33 (and_33_out, and_25_out, not_5_out);
  and and_34 (and_34_out, and_26_out, not_5_out);
  and and_35 (and_35_out, and_27_out, not_5_out);
  and and_36 (and_36_out, and_28_out, not_5_out);
  and and_37 (and_37_out, and_29_out, not_7_out);
  and and_38 (and_38_out, and_30_out, not_7_out);
  and and_39 (and_39_out, and_31_out, not_7_out);
  // And and_40 has open pins: In_1=and_32_out, In_2=not_7_out, out=open
  assign C_Arith[7] = or_17_out ? xor_32_out[7] : 1'bz;  // Driver driver_48
  or or_17 (or_17_out, and_33_out, and_34_out);

  // Notes on the sheet:
  //   B
  //   A
  //   ALU
  //   ADDER
  //   AND
  //   NAND
  //   OR
  //   NOR
  //   XOR
  //   .
  //   Z SWITCH
  //   3x8 Demux
  //   A1
  //   A2
  //   A3
  //   A_0
  //   2x4 Demux
  //   A_1
  //   Disable
endmodule

/* Test case:
C_2 C_1 C_0 A_0 B_0 C_Arith
0 0 0 9 6 15 #addition and subtraction
0 0 1 9 6 3
0 0 0 6 7 13
0 0 1 111 67 44
0 0 0 32 59 91
0 1 0 51 60 48  #and
0 1 0 3 2 2
0 1 0 5 3 1
0 1 0 12 25 8
0 1 0 4 8 0
1 0 0 5 3 7 #or
1 0 0 2 8 10
1 0 0 12 25 29
1 0 0 0 7 7
0 1 1 1 1 254 #nand
0 1 1 2 4 255
0 1 1 15 3 252
1 0 1 1 0 254 #nor
1 0 1 3 5 248
1 0 1 128 64 63
1 1 0 5 3 6 #xor
1 1 0 10 10 0
1 1 0 85 170 255
1 1 0 14 1 15
*/
