// Digital circuit CLA_Adder.dig as structural Verilog
module CLA_Adder (
  input  [7:0] B,
  input  [7:0] A,
  input  SUB,
  output [7:0] OUT
);

  wire and_1_out, and_2_out, and_3_out, and_4_out, and_5_out, and_6_out, and_7_out, and_8_out, and_9_out,
       and_10_out, and_11_out, and_12_out, and_13_out, and_14_out, and_15_out, and_16_out, and_17_out,
       and_18_out, and_19_out, and_20_out, and_21_out, and_22_out, and_23_out, and_24_out, and_25_out,
       and_26_out, and_27_out, and_28_out, and_29_out, and_30_out, and_31_out, and_32_out, and_33_out,
       and_34_out, and_35_out, and_36_out, and_37_out, and_38_out, and_39_out, and_40_out, and_41_out,
       and_42_out, and_43_out, and_44_out, and_45_out, and_46_out, and_47_out, and_48_out, or_1_out,
       or_2_out, or_3_out, or_4_out, or_5_out, or_6_out, or_7_out, or_8_out, or_9_out, or_10_out, or_11_out,
       or_12_out, or_13_out, or_14_out, or_15_out, or_16_out, or_17_out, or_18_out, or_19_out, or_20_out,
       xor_1_out, xor_2_out, xor_3_out, xor_4_out, xor_5_out, xor_6_out, xor_7_out, xor_8_out, xor_9_out,
       xor_10_out, xor_11_out, xor_12_out, xor_13_out, xor_14_out, xor_15_out, xor_16_out;

  xor xor_1 (xor_1_out, B[7], SUB);
  xor xor_2 (xor_2_out, B[6], SUB);
  xor xor_3 (xor_3_out, B[5], SUB);
  xor xor_4 (xor_4_out, SUB, B[4]);
  xor xor_5 (xor_5_out, SUB, B[3]);
  xor xor_6 (xor_6_out, SUB, B[2]);
  xor xor_7 (xor_7_out, SUB, B[1]);
  xor xor_8 (xor_8_out, SUB, B[0]);
  and and_1 (and_1_out, xor_1_out, A[7]);
  xor xor_9 (xor_9_out, xor_1_out, A[7]);
  and and_2 (and_2_out, xor_2_out, A[6]);
  xor xor_10 (xor_10_out, xor_2_out, A[6]);
  and and_3 (and_3_out, xor_3_out, A[5]);
  xor xor_11 (xor_11_out, xor_3_out, A[5]);
  and and_4 (and_4_out, xor_4_out, A[4]);
  xor xor_12 (xor_12_out, xor_4_out, A[4]);
  and and_5 (and_5_out, xor_5_out, A[3]);
  xor xor_13 (xor_13_out, xor_5_out, A[3]);
  and and_6 (and_6_out, xor_6_out, A[2]);
  xor xor_14 (xor_14_out, xor_6_out, A[2]);
  and and_7 (and_7_out, xor_7_out, A[1]);
  xor xor_15 (xor_15_out, xor_7_out, A[1]);
  and and_8 (and_8_out, xor_8_out, A[0]);
  xor xor_16 (xor_16_out, xor_8_out, A[0]);
  and and_9 (and_9_out, or_14_out, xor_12_out);
  and and_10 (and_10_out, xor_11_out, xor_10_out);
  and and_11 (and_11_out, and_3_out, xor_11_out);
  and and_12 (and_12_out, xor_10_out, xor_9_out);
  and and_13 (and_13_out, xor_9_out, xor_10_out);
  and and_14 (and_14_out, and_2_out, xor_9_out);
  and and_15 (and_15_out, xor_10_out, xor_11_out);
  and and_16 (and_16_out, xor_12_out, or_14_out);
  and and_17 (and_17_out, xor_11_out, xor_10_out);
  and and_18 (and_18_out, and_3_out, xor_10_out);
  and and_19 (and_19_out, xor_12_out, xor_11_out);
  and and_20 (and_20_out, xor_11_out, and_4_out);
  and and_21 (and_21_out, xor_12_out, or_14_out);
  and and_22 (and_22_out, SUB, xor_16_out);
  and and_23 (and_23_out, xor_15_out, xor_14_out);
  and and_24 (and_24_out, and_8_out, xor_15_out);
  and and_25 (and_25_out, xor_14_out, xor_13_out);
  and and_26 (and_26_out, xor_13_out, xor_14_out);
  and and_27 (and_27_out, and_6_out, xor_13_out);
  and and_28 (and_28_out, xor_14_out, xor_15_out);
  and and_29 (and_29_out, xor_16_out, SUB);
  and and_30 (and_30_out, xor_15_out, xor_14_out);
  and and_31 (and_31_out, and_7_out, xor_14_out);
  and and_32 (and_32_out, xor_16_out, xor_15_out);
  and and_33 (and_33_out, xor_15_out, and_8_out);
  and and_34 (and_34_out, xor_16_out, SUB);
  and and_35 (and_35_out, and_9_out, and_10_out);
  and and_36 (and_36_out, and_11_out, and_12_out);
  and and_37 (and_37_out, and_13_out, and_3_out);
  and and_38 (and_38_out, and_15_out, and_16_out);
  and and_39 (and_39_out, and_17_out, and_4_out);
  and and_40 (and_40_out, and_19_out, or_14_out);
  and and_41 (and_41_out, and_22_out, and_23_out);
  and and_42 (and_42_out, and_24_out, and_25_out);
  and and_43 (and_43_out, and_26_out, and_7_out);
  and and_44 (and_44_out, and_28_out, and_29_out);
  and and_45 (and_45_out, and_30_out, and_8_out);
  and and_46 (and_46_out, and_32_out, SUB);
  or or_1 (or_1_out, and_21_out, and_4_out);
  or or_2 (or_2_out, and_34_out, and_8_out);
  and and_47 (and_47_out, and_35_out, xor_9_out);
  or or_3 (or_3_out, and_40_out, and_20_out);
  and and_48 (and_48_out, and_41_out, xor_13_out);
  or or_4 (or_4_out, and_46_out, and_33_out);
  or or_5 (or_5_out, and_38_out, and_39_out);
  or or_6 (or_6_out, and_18_out, and_2_out);
  or or_7 (or_7_out, and_44_out, and_45_out);
  or or_8 (or_8_out, and_31_out, and_6_out);
  or or_9 (or_9_out, and_37_out, and_14_out);
  or or_10 (or_10_out, or_18_out, and_1_out);
  or or_11 (or_11_out, or_5_out, or_6_out);
  or or_12 (or_12_out, or_3_out, and_3_out);
  or or_13 (or_13_out, and_43_out, and_27_out);
  or or_14 (or_14_out, or_20_out, and_5_out);
  or or_15 (or_15_out, or_7_out, or_8_out);
  or or_16 (or_16_out, or_4_out, and_7_out);
  or or_17 (or_17_out, and_47_out, and_36_out);
  or or_18 (or_18_out, or_17_out, or_9_out);
  or or_19 (or_19_out, and_48_out, and_42_out);
  or or_20 (or_20_out, or_19_out, or_13_out);
  xor xor_17 (OUT[7], xor_9_out, or_11_out);
  xor xor_18 (OUT[6], xor_10_out, or_12_out);
  xor xor_19 (OUT[5], xor_11_out, or_1_out);
  xor xor_20 (OUT[4], or_14_out, xor_12_out);
  xor xor_21 (OUT[3], xor_13_out, or_15_out);
  xor xor_22 (OUT[2], xor_14_out, or_16_out);
  xor xor_23 (OUT[1], xor_15_out, or_2_out);
  xor xor_24 (OUT[0], SUB, xor_16_out);

  // Notes on the sheet:
  //   Generate
  //   Propogate
  //   4-bit Carry Look-ahead
  //   P_3
  //   G_3
  //   P_2
  //   G_2
  //   P_1
  //   G_1
  //   P_0
  //   C_0
  //   G_0
  //   5Inp
  //   4Inp
  //   3Inp
  //   .
  //   C_1
  //   C_4
  //   C_3
  //   C_2
endmodule

/* Test case:
# Random Test Suite
A B SUB OUT

# Add loop test
loop(i, 1000)
    let valA = random(256);
    let valB = random(256);
    (valA) (valB) 0 ((valA + valB) & 0xFF)
end loop

# Loop for Subtraction
loop(i, 1000)
    let valA = random(256);
    let valB = random(256);
    # (valA - valB) & 0xFF correctly handles 2's complement wrap-around
    (valA) (valB) 1 ((valA - valB) & 0xFF)
end loop
*/
