// Digital circuit LEG.dig as structural Verilog
module LEG (
  input  clk,
  input  [7:0] TestAdvRegister,
  input  [7:0] NormalRegTest,
  output [7:0] TAR_loadB,
  output [7:0] TAR_loadA,
  output [7:0] TAR_always,
  output [31:0] OPCODE_read,
  output [7:0] TAR_loadB_2,
  output [7:0] TAR_always_2,
  output [7:0] TAR_loadB_3,
  output [7:0] TAR_always_3,
  output [7:0] OPCODE,
  output [7:0] ARG1,
  output [7:0] ARG2,
  output [7:0] DESTINATION,
  output [7:0] ARG1_2,
  output [7:0] ARG2_2
);

  wire _74ffwithforceload_1_loaded_a, _74ffwithforceload_1_loaded_b, _74ffwithforceload_2_loaded_a,
       _74ffwithforceload_2_loaded_b, _74ffwithforceload_3_loaded_a, _74ffwithforceload_3_loaded_b,
       _74ffwithforceload_4_loaded_a, _74ffwithforceload_4_loaded_b, _74ffwithforceload_5_loaded_a,
       _74ffwithforceload_5_loaded_b, _74ffwithforceload_6_loaded_a, _74ffwithforceload_6_loaded_b,
       _74ffwithforceload_7_loaded_a, _74ffwithforceload_7_loaded_b, _74ffwithforceload_8_loaded_a,
       _74ffwithforceload_8_loaded_b, _74typeflipflop_17_always, _74typeflipflop_18_always,
       _74typeflipflop_19_always, _74typeflipflop_20_always, _74typeflipflop_21_always,
       _74typeflipflop_22_always, _74typeflipflop_23_always, _74typeflipflop_24_always,
       _74typeflipflop_25_always, _74typeflipflop_26_always, _74typeflipflop_27_always,
       _74typeflipflop_28_always, _74typeflipflop_29_always, _74typeflipflop_30_always,
       _74typeflipflop_31_always, _74typeflipflop_32_always, _74typeflipflop_33_always,
       _74typeflipflop_42_always, _74typeflipflop_43_always, _74typeflipflop_44_always,
       _74typeflipflop_45_always, _74typeflipflop_46_always, _74typeflipflop_47_always,
       _74typeflipflop_48_always, _74typeflipflop_49_always, _74typeflipflop_50_always,
       _74typeflipflop_51_always, _74typeflipflop_52_always, _74typeflipflop_53_always,
       _74typeflipflop_54_always, _74typeflipflop_55_always, _74typeflipflop_56_always,
       _74typeflipflop_57_always, _74typeflipflop_58_always, _74typeflipflop_59_always,
       _74typeflipflop_60_always, _74typeflipflop_61_always, _74typeflipflop_62_always,
       _74typeflipflop_63_always, _74typeflipflop_64_always, _74typeflipflop_65_always,
       _74typeflipflop_66_always, _74typeflipflop_67_always, _74typeflipflop_68_always,
       _74typeflipflop_69_always, _74typeflipflop_70_always, _74typeflipflop_71_always,
       _74typeflipflop_72_always, _74typeflipflop_73_always, and_1_out, and_2_out, and_3_out, and_4_out,
       and_5_out, and_6_out, and_7_out, and_8_out, and_9_out, and_10_out, and_11_out, and_12_out, and_13_out,
       and_14_out, and_15_out, and_16_out, and_17_out, and_18_out, and_19_out, and_20_out, and_21_out,
       and_22_out, and_23_out, and_24_out, and_25_out, and_26_out, and_27_out, and_28_out, and_29_out,
       and_30_out, and_31_out, and_32_out, and_33_out, and_34_out, and_35_out, and_36_out, and_37_out,
       and_38_out, and_39_out, and_40_out, and_41_out, and_42_out, and_43_out, and_44_out, and_45_out,
       and_47_out, and_48_out, and_50_out, and_51_out, and_52_out, and_55_out, and_56_out, and_57_out,
       and_59_out, and_60_out, and_62_out, and_63_out, and_64_out, and_65_out, and_66_out, and_67_out,
       and_68_out, and_69_out, and_70_out, and_73_out, and_74_out, and_75_out, and_76_out, and_78_out,
       and_79_out, and_80_out, and_82_out, and_83_out, and_85_out, and_86_out, and_88_out, and_89_out,
       and_90_out, and_91_out, and_92_out, and_93_out, and_94_out, and_95_out, and_97_out, and_98_out,
       and_100_out, and_101_out, and_102_out, and_105_out, and_106_out, and_107_out, and_109_out,
       and_110_out, and_112_out, and_113_out, and_114_out, and_115_out, and_116_out, and_117_out,
       and_118_out, and_119_out, and_121_out, and_122_out, and_123_out, and_124_out, and_125_out,
       and_126_out, and_127_out, and_128_out, and_130_out, and_131_out, and_132_out, and_133_out,
       and_134_out, and_135_out, and_136_out, and_137_out, and_138_out, and_139_out, and_140_out,
       and_141_out, and_142_out, and_143_out, and_144_out, and_145_out, and_146_out, and_147_out,
       and_148_out, and_149_out, and_150_out, and_151_out, and_152_out, and_153_out, and_154_out,
       and_155_out, and_159_out, and_160_out, and_161_out, and_162_out, and_163_out, and_164_out,
       and_165_out, and_166_out, and_167_out, and_168_out, and_169_out, and_170_out, and_172_out,
       and_173_out, and_176_out, and_177_out, and_178_out, and_179_out, and_180_out, and_181_out,
       and_182_out, and_183_out, and_184_out, and_185_out, and_186_out, and_187_out, and_188_out,
       and_189_out, and_190_out, and_191_out, and_192_out, and_193_out, and_194_out, and_195_out,
       and_196_out, and_197_out, and_198_out, and_199_out, and_200_out, and_201_out, and_202_out,
       and_203_out, and_204_out, and_205_out, and_206_out, and_207_out, and_208_out, and_209_out,
       and_210_out, and_211_out, and_212_out, and_213_out, and_214_out, and_215_out, and_216_out,
       and_217_out, and_218_out, and_219_out, and_220_out, and_221_out, and_222_out, and_223_out,
       and_224_out, and_225_out, and_226_out, and_227_out, and_228_out, and_229_out, and_230_out,
       and_232_out, and_233_out, and_234_out, and_235_out, and_236_out, and_237_out, and_238_out,
       and_239_out, and_240_out, and_241_out, and_242_out, and_243_out, and_244_out, and_245_out,
       and_246_out, and_248_out, and_249_out, and_250_out, and_251_out, and_252_out, and_253_out,
       and_254_out, and_255_out, and_256_out, and_257_out, and_258_out, and_259_out, and_260_out,
       and_261_out, and_262_out, and_263_out, and_264_out, and_265_out, and_266_out, and_267_out,
       and_268_out, and_269_out, and_270_out, and_271_out, and_272_out, and_273_out, and_274_out,
       and_275_out, and_276_out, and_277_out, and_278_out, and_279_out, and_280_out, and_281_out,
       and_282_out, and_283_out, and_284_out, and_285_out, and_286_out, and_287_out, and_288_out,
       and_289_out, and_290_out, and_291_out, and_292_out, and_293_out, and_294_out, and_295_out,
       and_296_out, and_297_out, and_298_out, and_299_out, and_301_out, and_302_out, and_303_out,
       and_304_out, and_305_out, and_306_out, and_307_out, and_308_out, and_309_out, and_310_out,
       and_311_out, and_312_out, and_313_out, and_314_out, and_315_out, and_316_out, and_317_out,
       and_318_out, and_319_out, and_320_out, and_321_out, and_322_out, and_323_out, and_324_out,
       and_325_out, and_326_out, and_327_out, and_328_out, and_329_out, and_330_out, and_331_out,
       and_332_out, and_333_out, and_334_out, and_335_out, button_1_out, delay_3_out, delay_4_out,
       dipswitch_1_out, dipswitch_2_out, dipswitch_3_out, dipswitch_4_out, dipswitch_5_out, dipswitch_6_out,
       dipswitch_7_out, dipswitch_8_out, dipswitch_9_out, dipswitch_10_out, dipswitch_11_out,
       dipswitch_12_out, driver_137_out, driver_138_out, driver_139_out, driver_140_out, driver_141_out,
       driver_142_out, driver_143_out, driver_144_out, driver_145_out, driver_146_out, driver_147_out,
       driver_148_out, driver_149_out, driver_150_out, driver_151_out, driver_152_out, driver_153_out,
       driver_154_out, driver_155_out, driver_156_out, driver_157_out, driver_158_out, driver_159_out,
       driver_160_out, nand_9_out, nand_10_out, nand_11_out, nand_12_out, nand_13_out, nand_14_out,
       nand_15_out, nand_16_out, nand_17_out, nand_18_out, nand_19_out, nand_20_out, nand_21_out,
       nand_22_out, nand_23_out, nand_24_out, nand_25_out, nand_26_out, nand_27_out, nand_28_out,
       nand_29_out, nand_30_out, nand_31_out, nand_32_out, nand_33_out, nand_34_out, nand_35_out,
       nand_36_out, nand_37_out, nand_38_out, nand_39_out, nand_40_out, nand_41_out, nand_42_out,
       nand_43_out, nand_44_out, nand_45_out, nand_46_out, nand_47_out, nand_48_out, nand_49_out,
       nand_50_out, nand_51_out, nand_52_out, nand_53_out, nand_54_out, nand_55_out, nand_56_out,
       nand_57_out, nand_58_out, nand_59_out, nand_60_out, nand_61_out, nand_62_out, nand_63_out,
       nand_64_out, nor_9_out, nor_10_out, nor_11_out, nor_12_out, nor_13_out, nor_14_out, nor_15_out,
       nor_16_out, nor_17_out, nor_18_out, nor_19_out, nor_20_out, nor_21_out, nor_22_out, nor_23_out,
       nor_24_out, nor_25_out, nor_26_out, nor_27_out, nor_28_out, nor_29_out, nor_30_out, nor_31_out,
       nor_32_out, nor_33_out, nor_34_out, not_1_out, not_2_out, not_3_out, not_4_out, not_5_out, not_6_out,
       not_7_out, not_8_out, not_9_out, not_10_out, not_11_out, not_12_out, not_13_out, not_14_out,
       not_15_out, not_16_out, not_17_out, not_18_out, not_19_out, not_20_out, not_21_out, not_22_out,
       not_23_out, not_24_out, not_25_out, not_26_out, not_27_out, not_28_out, not_29_out, not_30_out,
       not_31_out, not_32_out, not_33_out, not_34_out, not_35_out, not_36_out, not_37_out, not_38_out,
       not_39_out, not_40_out, not_41_out, not_42_out, not_43_out, not_44_out, not_45_out, not_46_out,
       not_47_out, not_48_out, not_49_out, not_50_out, not_51_out, not_52_out, not_53_out, not_54_out,
       not_55_out, not_56_out, not_57_out, not_58_out, not_59_out, not_60_out, not_61_out, not_62_out,
       not_63_out, not_64_out, not_65_out, not_66_out, not_67_out, not_68_out, notconnected_7_out,
       notconnected_8_out, notconnected_12_out, notconnected_17_out, notconnected_21_out,
       notconnected_22_out, notconnected_23_out, notconnected_24_out, notconnected_26_out, or_1_out,
       or_3_out, or_4_out, or_5_out, or_6_out, or_7_out, or_8_out, or_9_out, or_10_out, or_11_out, or_12_out,
       or_13_out, or_14_out, or_15_out, or_21_out, or_22_out, or_26_out, or_27_out, or_28_out, or_29_out,
       or_30_out, or_31_out, or_32_out, or_33_out, or_34_out, or_35_out, or_36_out, or_37_out, or_38_out,
       or_39_out, or_40_out, or_41_out, or_42_out, or_43_out, or_44_out, or_45_out, or_46_out, or_47_out,
       or_48_out, or_49_out, or_50_out, or_51_out, or_52_out, or_53_out, or_54_out, or_55_out, or_56_out,
       or_57_out, or_58_out, or_59_out, or_60_out, or_61_out, or_62_out, or_63_out, or_64_out, or_65_out,
       or_66_out, or_67_out, or_68_out, or_69_out, or_70_out, or_71_out, or_72_out, or_73_out, or_74_out,
       or_75_out, or_76_out, or_77_out, or_78_out, or_79_out, or_80_out, or_81_out, or_82_out, or_83_out,
       or_84_out, or_85_out, or_86_out, or_87_out, or_88_out, or_89_out, or_90_out, or_91_out, or_92_out,
       or_93_out, or_94_out, or_95_out, reset_1_out, reset_2_out, reset_3_out, reset_4_out, reset_5_out,
       reset_6_out, reset_7_out, reset_8_out, reset_9_out, reset_10_out, reset_11_out, reset_21_out,
       undriven, xor_1_out, xor_2_out, xor_3_out, xor_4_out, xor_5_out, xor_6_out, xor_7_out, xor_8_out,
       xor_17_out, xor_18_out, xor_19_out, xor_20_out, xor_21_out, xor_22_out, xor_23_out, xor_24_out,
       xor_25_out, xor_26_out, xor_27_out, xor_28_out, xor_29_out, xor_30_out, xor_31_out, xor_32_out,
       xor_33_out, xor_34_out, xor_35_out, xor_36_out, xor_37_out, xor_38_out, xor_39_out, xor_40_out,
       xor_42_out, xor_43_out, xor_44_out, xor_45_out, xor_46_out, xor_47_out, xor_48_out, xor_49_out,
       xor_73_out, xor_74_out, xor_75_out, xor_76_out, xor_77_out, xor_78_out, xor_79_out, xor_80_out,
       xor_81_out, xor_82_out, xor_83_out, xor_84_out, xor_85_out, xor_86_out, xor_87_out, xor_88_out,
       xor_89_out, xor_90_out, xor_91_out, xor_92_out, xor_93_out, xor_94_out, xor_95_out, xor_96_out,
       xor_97_out, xor_98_out, xor_99_out, xor_100_out, xor_101_out, xor_102_out, xor_103_out, xor_104_out;
  wire [5:0] and_61_out, delay_2_out;
  wire [7:0] _74ffwithforceload_8_always, _74typeflipflop_8_loaded_a, _74typeflipflop_16_loaded_a,
       _74typeflipflop_25_loaded_a, _74typeflipflop_25_loaded_b, _74typeflipflop_41_always, and_87_out,
       and_111_out, and_175_out, delay_1_out, driver_14_out, driver_24_out, driver_33_out, driver_48_out,
       driver_116_out, nand_8_out, nor_8_out, notconnected_5_out, notconnected_9_out, notconnected_10_out,
       notconnected_11_out, notconnected_13_out, notconnected_14_out, notconnected_15_out,
       notconnected_16_out, notconnected_18_out, notconnected_19_out, notconnected_20_out,
       notconnected_25_out, or_25_out, pulldown_1_out, rom_1_d, xnor_14_out, xnor_16_out, xor_16_out,
       xor_56_out, xor_57_out, xor_69_out;

  assign driver_14_out[0] = and_39_out ? _74typeflipflop_8_loaded_a[0] : 1'bz;  // Driver driver_1
  assign driver_14_out[1] = and_39_out ? _74typeflipflop_8_loaded_a[1] : 1'bz;  // Driver driver_2
  assign driver_14_out[0] = not_1_out ? DESTINATION[0] : 1'bz;  // Driver driver_3
  assign driver_14_out[1] = not_1_out ? DESTINATION[1] : 1'bz;  // Driver driver_4
  assign driver_14_out[2] = and_39_out ? _74typeflipflop_8_loaded_a[2] : 1'bz;  // Driver driver_5
  assign driver_14_out[3] = and_39_out ? _74typeflipflop_8_loaded_a[3] : 1'bz;  // Driver driver_6
  assign driver_14_out[2] = not_1_out ? DESTINATION[2] : 1'bz;  // Driver driver_7
  assign driver_14_out[3] = not_1_out ? DESTINATION[3] : 1'bz;  // Driver driver_8
  assign driver_14_out[4] = and_39_out ? _74typeflipflop_8_loaded_a[4] : 1'bz;  // Driver driver_9
  assign driver_14_out[5] = and_39_out ? _74typeflipflop_8_loaded_a[5] : 1'bz;  // Driver driver_10
  assign driver_14_out[4] = not_1_out ? DESTINATION[4] : 1'bz;  // Driver driver_11
  assign driver_14_out[5] = not_1_out ? DESTINATION[5] : 1'bz;  // Driver driver_12
  assign driver_14_out[6] = and_39_out ? _74typeflipflop_8_loaded_a[6] : 1'bz;  // Driver driver_13
  assign driver_14_out[7] = and_39_out ? _74typeflipflop_8_loaded_a[7] : 1'bz;  // Driver driver_14
  assign driver_14_out[6] = not_1_out ? DESTINATION[6] : 1'bz;  // Driver driver_15
  assign driver_14_out[7] = not_1_out ? DESTINATION[7] : 1'bz;  // Driver driver_16
  not not_1 (not_1_out, and_39_out);
  or or_1 (or_1_out, and_248_out, and_39_out);
  and and_1 (and_1_out, 1'b0, _74ffwithforceload_8_always[7]);
  xor xor_1 (xor_1_out, _74ffwithforceload_8_always[7], 1'b0);
  and and_2 (and_2_out, 1'b0, _74ffwithforceload_8_always[6]);
  xor xor_2 (xor_2_out, _74ffwithforceload_8_always[6], 1'b0);
  and and_3 (and_3_out, 1'b0, _74ffwithforceload_8_always[5]);
  xor xor_3 (xor_3_out, _74ffwithforceload_8_always[5], 1'b0);
  and and_4 (and_4_out, 1'b0, _74ffwithforceload_8_always[4]);
  xor xor_4 (xor_4_out, _74ffwithforceload_8_always[4], 1'b0);
  and and_5 (and_5_out, 1'b0, _74ffwithforceload_8_always[3]);
  xor xor_5 (xor_5_out, _74ffwithforceload_8_always[3], 1'b0);
  and and_6 (and_6_out, 1'b0, _74ffwithforceload_8_always[2]);
  xor xor_6 (xor_6_out, _74ffwithforceload_8_always[2], 1'b0);
  and and_7 (and_7_out, 1'b0, _74ffwithforceload_8_always[1]);
  xor xor_7 (xor_7_out, _74ffwithforceload_8_always[1], 1'b0);
  and and_8 (and_8_out, 1'b1, _74ffwithforceload_8_always[0]);
  xor xor_8 (xor_8_out, _74ffwithforceload_8_always[0], 1'b1);
  assign driver_24_out[0] = or_1_out ? driver_14_out[0] : 1'bz;  // Driver driver_17
  // Or or_2 has open pins: In_1=and_1_out, In_2=and_9_out, out=open
  and and_9 (and_9_out, xor_1_out, or_3_out);
  xor xor_9 (xor_16_out[7], xor_1_out, or_3_out);
  or or_3 (or_3_out, and_2_out, and_10_out);
  and and_10 (and_10_out, xor_2_out, or_4_out);
  xor xor_10 (xor_16_out[6], xor_2_out, or_4_out);
  or or_4 (or_4_out, and_3_out, and_11_out);
  and and_11 (and_11_out, xor_3_out, or_5_out);
  xor xor_11 (xor_16_out[5], xor_3_out, or_5_out);
  or or_5 (or_5_out, and_4_out, and_12_out);
  and and_12 (and_12_out, xor_4_out, or_6_out);
  xor xor_12 (xor_16_out[4], xor_4_out, or_6_out);
  or or_6 (or_6_out, and_5_out, and_13_out);
  or or_7 (or_7_out, and_6_out, and_14_out);
  or or_8 (or_8_out, and_7_out, and_15_out);
  or or_9 (or_9_out, and_8_out, and_16_out);
  assign driver_24_out[1] = or_1_out ? driver_14_out[1] : 1'bz;  // Driver driver_18
  assign driver_24_out[2] = or_1_out ? driver_14_out[2] : 1'bz;  // Driver driver_19
  and and_13 (and_13_out, xor_5_out, or_7_out);
  xor xor_13 (xor_16_out[3], xor_5_out, or_7_out);
  and and_14 (and_14_out, xor_6_out, or_8_out);
  xor xor_14 (xor_16_out[2], xor_6_out, or_8_out);
  and and_15 (and_15_out, xor_7_out, or_9_out);
  xor xor_15 (xor_16_out[1], xor_7_out, or_9_out);
  and and_16 (and_16_out, xor_8_out, 1'b0);
  xor xor_16 (xor_16_out[0], xor_8_out, 1'b0);
  assign driver_24_out[3] = or_1_out ? driver_14_out[3] : 1'bz;  // Driver driver_20
  assign driver_24_out[4] = or_1_out ? driver_14_out[4] : 1'bz;  // Driver driver_21
  assign driver_24_out[5] = or_1_out ? driver_14_out[5] : 1'bz;  // Driver driver_22
  assign driver_24_out[6] = or_1_out ? driver_14_out[6] : 1'bz;  // Driver driver_23
  not not_2 (not_2_out, or_1_out);
  assign driver_24_out[7] = or_1_out ? driver_14_out[7] : 1'bz;  // Driver driver_24
  assign driver_24_out[0] = not_2_out ? xor_16_out[0] : 1'bz;  // Driver driver_25
  assign driver_24_out[1] = not_2_out ? xor_16_out[1] : 1'bz;  // Driver driver_26
  assign driver_24_out[2] = not_2_out ? xor_16_out[2] : 1'bz;  // Driver driver_27
  assign driver_24_out[3] = not_2_out ? xor_16_out[3] : 1'bz;  // Driver driver_28
  assign driver_24_out[4] = not_2_out ? xor_16_out[4] : 1'bz;  // Driver driver_29
  assign driver_24_out[5] = not_2_out ? xor_16_out[5] : 1'bz;  // Driver driver_30
  and and_17 (and_17_out, not_7_out, not_5_out);
  not not_3 (not_3_out, and_17_out);
  assign driver_24_out[6] = not_2_out ? xor_16_out[6] : 1'bz;  // Driver driver_31
  assign driver_24_out[7] = not_2_out ? xor_16_out[7] : 1'bz;  // Driver driver_32
  not not_4 (not_4_out, _74typeflipflop_17_always);
  Delay #(.Bits(8), .delayTime(5)) delay_1 (.in(pulldown_1_out), .out(delay_1_out));
  PullDown #(.Bits(8)) pulldown_1 (.out(pulldown_1_out));
  and and_18 (and_18_out, not_3_out, not_4_out);
  and and_19 (and_19_out, not_3_out, not_4_out);
  Delay #(.Bits(6), .delayTime(5)) delay_2 (.in(and_61_out), .out(delay_2_out));
  Delay #(.delayTime(3)) delay_3 (.in(and_19_out), .out(delay_3_out));
  DipSwitch dipswitch_1 (.out(dipswitch_1_out));
  Reset #(.invertOutput("false")) reset_1 (.out(reset_1_out));
  DipSwitch dipswitch_2 (.out(dipswitch_2_out));
  Reset #(.invertOutput("false")) reset_2 (.out(reset_2_out));
  not not_5 (not_5_out, clk);
  not not_6 (not_6_out, clk);
  Reset #(.invertOutput("false")) reset_3 (.out(reset_3_out));
  Reset #(.invertOutput("false")) reset_4 (.out(reset_4_out));
  _74TypeFlipFlop _74typeflipflop_1 (
    .CLK(and_17_out), .Data(delay_1_out[7]), .Load_A(and_18_out), .Load_B(dipswitch_1_out),
    .Always(TAR_always_2[7]), .Loaded_A(_74typeflipflop_8_loaded_a[7]), .Loaded_B(TAR_loadB_2[7]),
    .Reset(reset_1_out));
  _74TypeFlipFlop _74typeflipflop_2 (
    .CLK(and_17_out), .Data(delay_1_out[6]), .Load_A(and_18_out), .Load_B(dipswitch_1_out),
    .Always(TAR_always_2[6]), .Loaded_A(_74typeflipflop_8_loaded_a[6]), .Loaded_B(TAR_loadB_2[6]),
    .Reset(reset_1_out));
  _74TypeFlipFlop _74typeflipflop_3 (
    .CLK(and_17_out), .Data(delay_1_out[5]), .Load_A(and_18_out), .Load_B(dipswitch_1_out),
    .Always(TAR_always_2[5]), .Loaded_A(_74typeflipflop_8_loaded_a[5]), .Loaded_B(TAR_loadB_2[5]),
    .Reset(reset_1_out));
  _74TypeFlipFlop _74typeflipflop_4 (
    .CLK(and_17_out), .Data(delay_1_out[4]), .Load_A(and_18_out), .Load_B(dipswitch_1_out),
    .Always(TAR_always_2[4]), .Loaded_A(_74typeflipflop_8_loaded_a[4]), .Loaded_B(TAR_loadB_2[4]),
    .Reset(reset_1_out));
  _74TypeFlipFlop _74typeflipflop_5 (
    .CLK(and_17_out), .Data(delay_1_out[3]), .Load_A(and_18_out), .Load_B(dipswitch_1_out),
    .Always(TAR_always_2[3]), .Loaded_A(_74typeflipflop_8_loaded_a[3]), .Loaded_B(TAR_loadB_2[3]),
    .Reset(reset_1_out));
  _74TypeFlipFlop _74typeflipflop_6 (
    .CLK(and_17_out), .Data(delay_1_out[2]), .Load_A(and_18_out), .Load_B(dipswitch_1_out),
    .Always(TAR_always_2[2]), .Loaded_A(_74typeflipflop_8_loaded_a[2]), .Loaded_B(TAR_loadB_2[2]),
    .Reset(reset_1_out));
  _74TypeFlipFlop _74typeflipflop_7 (
    .CLK(and_17_out), .Data(delay_1_out[1]), .Load_A(and_18_out), .Load_B(dipswitch_1_out),
    .Always(TAR_always_2[1]), .Loaded_A(_74typeflipflop_8_loaded_a[1]), .Loaded_B(TAR_loadB_2[1]),
    .Reset(reset_1_out));
  _74TypeFlipFlop _74typeflipflop_8 (
    .CLK(and_17_out), .Data(delay_1_out[0]), .Load_A(and_18_out), .Load_B(dipswitch_1_out),
    .Always(TAR_always_2[0]), .Loaded_A(_74typeflipflop_8_loaded_a[0]), .Loaded_B(TAR_loadB_2[0]),
    .Reset(reset_1_out));
  _74TypeFlipFlop _74typeflipflop_9 (
    .CLK(and_17_out), .Data(1'b0), .Load_A(delay_3_out), .Load_B(dipswitch_2_out), .Always(TAR_always_3[7]),
    .Loaded_A(_74typeflipflop_16_loaded_a[7]), .Loaded_B(TAR_loadB_3[7]), .Reset(reset_2_out));
  _74TypeFlipFlop _74typeflipflop_10 (
    .CLK(and_17_out), .Data(1'b0), .Load_A(delay_3_out), .Load_B(dipswitch_2_out), .Always(TAR_always_3[6]),
    .Loaded_A(_74typeflipflop_16_loaded_a[6]), .Loaded_B(TAR_loadB_3[6]), .Reset(reset_2_out));
  _74TypeFlipFlop _74typeflipflop_11 (
    .CLK(and_17_out), .Data(delay_2_out[5]), .Load_A(delay_3_out), .Load_B(dipswitch_2_out),
    .Always(TAR_always_3[5]), .Loaded_A(_74typeflipflop_16_loaded_a[5]), .Loaded_B(TAR_loadB_3[5]),
    .Reset(reset_2_out));
  _74TypeFlipFlop _74typeflipflop_12 (
    .CLK(and_17_out), .Data(delay_2_out[4]), .Load_A(delay_3_out), .Load_B(dipswitch_2_out),
    .Always(TAR_always_3[4]), .Loaded_A(_74typeflipflop_16_loaded_a[4]), .Loaded_B(TAR_loadB_3[4]),
    .Reset(reset_2_out));
  _74TypeFlipFlop _74typeflipflop_13 (
    .CLK(and_17_out), .Data(delay_2_out[3]), .Load_A(delay_3_out), .Load_B(dipswitch_2_out),
    .Always(TAR_always_3[3]), .Loaded_A(_74typeflipflop_16_loaded_a[3]), .Loaded_B(TAR_loadB_3[3]),
    .Reset(reset_2_out));
  _74TypeFlipFlop _74typeflipflop_14 (
    .CLK(and_17_out), .Data(delay_2_out[2]), .Load_A(delay_3_out), .Load_B(dipswitch_2_out),
    .Always(TAR_always_3[2]), .Loaded_A(_74typeflipflop_16_loaded_a[2]), .Loaded_B(TAR_loadB_3[2]),
    .Reset(reset_2_out));
  _74TypeFlipFlop _74typeflipflop_15 (
    .CLK(and_17_out), .Data(delay_2_out[1]), .Load_A(delay_3_out), .Load_B(dipswitch_2_out),
    .Always(TAR_always_3[1]), .Loaded_A(_74typeflipflop_16_loaded_a[1]), .Loaded_B(TAR_loadB_3[1]),
    .Reset(reset_2_out));
  _74TypeFlipFlop _74typeflipflop_16 (
    .CLK(and_17_out), .Data(delay_2_out[0]), .Load_A(delay_3_out), .Load_B(dipswitch_2_out),
    .Always(TAR_always_3[0]), .Loaded_A(_74typeflipflop_16_loaded_a[0]), .Loaded_B(TAR_loadB_3[0]),
    .Reset(reset_2_out));
  Delay delay_4 (.in(reset_4_out), .out(delay_4_out));
  assign driver_33_out[0] = and_27_out ? TAR_always_2[0] : 1'bz;  // Driver driver_33
  or or_10 (or_10_out, and_248_out, and_39_out);
  or or_11 (or_11_out, reset_4_out, and_43_out);
  assign driver_33_out[1] = and_27_out ? TAR_always_2[1] : 1'bz;  // Driver driver_34
  assign driver_33_out[2] = and_27_out ? TAR_always_2[2] : 1'bz;  // Driver driver_35
  or or_12 (or_12_out, delay_4_out, not_5_out);
  or or_13 (or_13_out, or_10_out, or_11_out);
  and and_20 (and_20_out, xnor_16_out[1], xnor_16_out[0]);
  and and_21 (and_21_out, and_22_out, and_20_out);
  assign driver_33_out[3] = and_27_out ? TAR_always_2[3] : 1'bz;  // Driver driver_36
  assign driver_33_out[4] = and_27_out ? TAR_always_2[4] : 1'bz;  // Driver driver_37
  _74TypeFlipFlop _74typeflipflop_17 (
    .CLK(or_12_out), .Data(or_13_out), .Load_A(1'b0), .Load_B(1'b0), .Always(_74typeflipflop_17_always),
    .Reset(1'b0));  // open: Loaded_A, Loaded_B
  and and_22 (and_22_out, xnor_16_out[3], xnor_16_out[2]);
  and and_23 (and_23_out, and_26_out, and_21_out);
  and and_24 (and_24_out, _74typeflipflop_17_always, and_23_out);
  assign driver_33_out[5] = and_27_out ? TAR_always_2[5] : 1'bz;  // Driver driver_38
  assign driver_33_out[6] = and_27_out ? TAR_always_2[6] : 1'bz;  // Driver driver_39
  _74FFWithForceLoad _74ffwithforceload_1 (
    .CLK(not_6_out), .D(driver_24_out[7]), .Load_A(1'b0), .Load_B(1'b0),
    .Always(_74ffwithforceload_8_always[7]), .Loaded_A(_74ffwithforceload_1_loaded_a),
    .Loaded_B(_74ffwithforceload_1_loaded_b), .CLR(reset_3_out), .PRE(undriven));
  _74FFWithForceLoad _74ffwithforceload_2 (
    .CLK(not_6_out), .D(driver_24_out[6]), .Load_A(1'b0), .Load_B(1'b0),
    .Always(_74ffwithforceload_8_always[6]), .Loaded_A(_74ffwithforceload_2_loaded_a),
    .Loaded_B(_74ffwithforceload_2_loaded_b), .CLR(reset_3_out), .PRE(undriven));
  _74FFWithForceLoad _74ffwithforceload_3 (
    .CLK(not_6_out), .D(driver_24_out[5]), .Load_A(1'b0), .Load_B(1'b0),
    .Always(_74ffwithforceload_8_always[5]), .Loaded_A(_74ffwithforceload_3_loaded_a),
    .Loaded_B(_74ffwithforceload_3_loaded_b), .CLR(reset_3_out), .PRE(undriven));
  _74FFWithForceLoad _74ffwithforceload_4 (
    .CLK(not_6_out), .D(driver_24_out[4]), .Load_A(1'b0), .Load_B(1'b0),
    .Always(_74ffwithforceload_8_always[4]), .Loaded_A(_74ffwithforceload_4_loaded_a),
    .Loaded_B(_74ffwithforceload_4_loaded_b), .CLR(reset_3_out), .PRE(undriven));
  _74FFWithForceLoad _74ffwithforceload_5 (
    .CLK(not_6_out), .D(driver_24_out[3]), .Load_A(1'b0), .Load_B(1'b0),
    .Always(_74ffwithforceload_8_always[3]), .Loaded_A(_74ffwithforceload_5_loaded_a),
    .Loaded_B(_74ffwithforceload_5_loaded_b), .CLR(reset_3_out), .PRE(undriven));
  _74FFWithForceLoad _74ffwithforceload_6 (
    .CLK(not_6_out), .D(driver_24_out[2]), .Load_A(1'b0), .Load_B(1'b0),
    .Always(_74ffwithforceload_8_always[2]), .Loaded_A(_74ffwithforceload_6_loaded_a),
    .Loaded_B(_74ffwithforceload_6_loaded_b), .CLR(reset_3_out), .PRE(undriven));
  _74FFWithForceLoad _74ffwithforceload_7 (
    .CLK(not_6_out), .D(driver_24_out[1]), .Load_A(1'b0), .Load_B(1'b0),
    .Always(_74ffwithforceload_8_always[1]), .Loaded_A(_74ffwithforceload_7_loaded_a),
    .Loaded_B(_74ffwithforceload_7_loaded_b), .CLR(reset_3_out), .PRE(undriven));
  _74FFWithForceLoad _74ffwithforceload_8 (
    .CLK(not_6_out), .D(driver_24_out[0]), .Load_A(1'b0), .Load_B(1'b0),
    .Always(_74ffwithforceload_8_always[0]), .Loaded_A(_74ffwithforceload_8_loaded_a),
    .Loaded_B(_74ffwithforceload_8_loaded_b), .CLR(reset_3_out));  // open: PRE
  xnor xnor_1 (xnor_14_out[0], TAR_always_3[0], and_87_out[0]);
  xnor xnor_2 (xnor_16_out[0], TAR_always_3[0], and_111_out[0]);
  and and_25 (and_25_out, xnor_16_out[5], xnor_16_out[4]);
  and and_26 (and_26_out, and_28_out, and_25_out);
  and and_27 (and_27_out, not_8_out, and_24_out);
  assign driver_33_out[7] = and_27_out ? TAR_always_2[7] : 1'bz;  // Driver driver_40
  xnor xnor_3 (xnor_14_out[1], TAR_always_3[1], and_87_out[1]);
  xnor xnor_4 (xnor_16_out[1], TAR_always_3[1], and_111_out[1]);
  and and_28 (and_28_out, xnor_16_out[7], xnor_16_out[6]);
  xnor xnor_5 (xnor_14_out[2], TAR_always_3[2], and_87_out[2]);
  xnor xnor_6 (xnor_14_out[3], TAR_always_3[3], and_87_out[3]);
  xnor xnor_7 (xnor_16_out[2], TAR_always_3[2], and_111_out[2]);
  xnor xnor_8 (xnor_16_out[3], TAR_always_3[3], and_111_out[3]);
  and and_29 (and_29_out, xnor_14_out[1], xnor_14_out[0]);
  assign driver_48_out[0] = and_37_out ? TAR_always_2[0] : 1'bz;  // Driver driver_41
  xnor xnor_9 (xnor_14_out[4], TAR_always_3[4], and_87_out[4]);
  xnor xnor_10 (xnor_16_out[4], TAR_always_3[4], and_111_out[4]);
  and and_30 (and_30_out, xnor_14_out[3], xnor_14_out[2]);
  and and_31 (and_31_out, and_30_out, and_29_out);
  and and_32 (and_32_out, _74typeflipflop_17_always, and_34_out);
  assign driver_48_out[1] = and_37_out ? TAR_always_2[1] : 1'bz;  // Driver driver_42
  assign driver_48_out[2] = and_37_out ? TAR_always_2[2] : 1'bz;  // Driver driver_43
  xnor xnor_11 (xnor_14_out[5], TAR_always_3[5], and_87_out[5]);
  xnor xnor_12 (xnor_16_out[5], TAR_always_3[5], and_111_out[5]);
  and and_33 (and_33_out, xnor_14_out[5], xnor_14_out[4]);
  and and_34 (and_34_out, and_36_out, and_31_out);
  assign driver_48_out[3] = and_37_out ? TAR_always_2[3] : 1'bz;  // Driver driver_44
  assign driver_48_out[4] = and_37_out ? TAR_always_2[4] : 1'bz;  // Driver driver_45
  xnor xnor_13 (xnor_14_out[6], TAR_always_3[6], and_87_out[6]);
  xnor xnor_14 (xnor_14_out[7], TAR_always_3[7], and_87_out[7]);
  xnor xnor_15 (xnor_16_out[6], TAR_always_3[6], and_111_out[6]);
  xnor xnor_16 (xnor_16_out[7], TAR_always_3[7], and_111_out[7]);
  and and_35 (and_35_out, xnor_14_out[7], xnor_14_out[6]);
  and and_36 (and_36_out, and_35_out, and_33_out);
  and and_37 (and_37_out, not_9_out, and_32_out);
  assign driver_48_out[5] = and_37_out ? TAR_always_2[5] : 1'bz;  // Driver driver_46
  assign driver_48_out[6] = and_37_out ? TAR_always_2[6] : 1'bz;  // Driver driver_47
  PullDown pulldown_2 (.out(_74typeflipflop_16_loaded_a[1]));
  PullDown pulldown_3 (.out(_74typeflipflop_16_loaded_a[0]));
  assign driver_48_out[7] = and_37_out ? TAR_always_2[7] : 1'bz;  // Driver driver_48
  not not_7 (not_7_out, and_248_out);
  PullDown pulldown_4 (.out(_74typeflipflop_16_loaded_a[5]));
  PullDown pulldown_5 (.out(_74typeflipflop_16_loaded_a[4]));
  PullDown pulldown_6 (.out(_74typeflipflop_16_loaded_a[3]));
  PullDown pulldown_7 (.out(_74typeflipflop_16_loaded_a[2]));
  PullDown pulldown_8 (.out(_74typeflipflop_16_loaded_a[7]));
  PullDown pulldown_9 (.out(_74typeflipflop_16_loaded_a[6]));
  not not_8 (not_8_out, OPCODE[7]);
  not not_9 (not_9_out, OPCODE[6]);
  not not_10 (not_10_out, DESTINATION[2]);
  not not_11 (not_11_out, not_10_out);
  and and_38 (and_38_out, and_41_out, not_11_out);
  and and_39 (and_39_out, not_17_out, and_38_out);
  and and_40 (and_40_out, not_13_out, DESTINATION[1]);
  and and_41 (and_41_out, DESTINATION[1], DESTINATION[0]);
  and and_42 (and_42_out, and_40_out, not_11_out);
  and and_43 (and_43_out, not_17_out, and_42_out);
  ROM #(.AddrBits(8), .isProgramMemory("true"), .Bits(32)) Program_Memory (
    .A(_74ffwithforceload_8_always), .sel(clk), .D({OPCODE, ARG1, ARG2, DESTINATION}));
  and and_44 (and_44_out, DESTINATION[0], not_12_out);
  and and_45 (and_45_out, and_44_out, not_11_out);
  and and_46 (and_61_out[5], not_17_out, and_45_out);
  and and_47 (and_47_out, not_13_out, not_12_out);
  and and_48 (and_48_out, and_47_out, not_11_out);
  and and_49 (and_61_out[4], not_17_out, and_48_out);
  not not_12 (not_12_out, DESTINATION[1]);
  not not_13 (not_13_out, DESTINATION[0]);
  not not_14 (not_14_out, DESTINATION[2]);
  and and_50 (and_50_out, DESTINATION[1], DESTINATION[0]);
  and and_51 (and_51_out, and_56_out, not_14_out);
  and and_52 (and_52_out, and_50_out, not_14_out);
  and and_53 (and_61_out[2], not_17_out, and_51_out);
  and and_54 (and_61_out[3], not_17_out, and_52_out);
  and and_55 (and_55_out, DESTINATION[0], not_15_out);
  and and_56 (and_56_out, not_16_out, DESTINATION[1]);
  and and_57 (and_57_out, and_55_out, not_14_out);
  and and_58 (and_61_out[1], not_17_out, and_57_out);
  and and_59 (and_59_out, not_16_out, not_15_out);
  and and_60 (and_60_out, and_59_out, not_14_out);
  and and_61 (and_61_out[0], not_17_out, and_60_out);
  not not_15 (not_15_out, DESTINATION[1]);
  not not_16 (not_16_out, DESTINATION[0]);
  not not_17 (not_17_out, and_248_out);
  _74TypeFlipFlop _74typeflipflop_18 (
    .CLK(and_43_out), .Data(pulldown_1_out[7]), .Load_A(dipswitch_3_out), .Load_B(dipswitch_4_out),
    .Always(_74typeflipflop_18_always), .Loaded_A(_74typeflipflop_25_loaded_a[7]),
    .Loaded_B(_74typeflipflop_25_loaded_b[7]), .Reset(reset_5_out));
  _74TypeFlipFlop _74typeflipflop_19 (
    .CLK(and_43_out), .Data(pulldown_1_out[6]), .Load_A(dipswitch_3_out), .Load_B(dipswitch_4_out),
    .Always(_74typeflipflop_19_always), .Loaded_A(_74typeflipflop_25_loaded_a[6]),
    .Loaded_B(_74typeflipflop_25_loaded_b[6]), .Reset(reset_5_out));
  PullDown #(.Bits(32)) pulldown_10 (.out({OPCODE, ARG1, ARG2, DESTINATION}));
  LED led_1 (.in(_74typeflipflop_18_always));
  LED led_2 (.in(_74typeflipflop_18_always));
  LED led_3 (.in(_74typeflipflop_18_always));
  LED led_4 (.in(_74typeflipflop_18_always));
  LED led_5 (.in(_74typeflipflop_18_always));
  LED led_6 (.in(_74typeflipflop_18_always));
  LED led_7 (.in(_74typeflipflop_18_always));
  LED led_8 (.in(_74typeflipflop_18_always));
  not not_18 (not_18_out, ARG2[2]);
  not not_19 (not_19_out, not_18_out);
  and and_62 (and_62_out, ARG2[1], ARG2[0]);
  and and_63 (and_63_out, and_62_out, not_19_out);
  and and_64 (and_64_out, not_27_out, and_63_out);
  LED led_9 (.in(_74typeflipflop_18_always));
  LED led_10 (.in(_74typeflipflop_18_always));
  LED led_11 (.in(_74typeflipflop_18_always));
  LED led_12 (.in(_74typeflipflop_18_always));
  LED led_13 (.in(_74typeflipflop_18_always));
  LED led_14 (.in(_74typeflipflop_18_always));
  LED led_15 (.in(_74typeflipflop_18_always));
  LED led_16 (.in(_74typeflipflop_18_always));
  LED led_17 (.in(_74typeflipflop_18_always));
  LED led_18 (.in(_74typeflipflop_18_always));
  LED led_19 (.in(_74typeflipflop_18_always));
  LED led_20 (.in(_74typeflipflop_18_always));
  LED led_21 (.in(_74typeflipflop_18_always));
  LED led_22 (.in(_74typeflipflop_18_always));
  LED led_23 (.in(_74typeflipflop_18_always));
  LED led_24 (.in(_74typeflipflop_18_always));
  and and_65 (and_65_out, not_21_out, ARG2[1]);
  and and_66 (and_66_out, and_65_out, not_19_out);
  and and_67 (and_67_out, not_27_out, and_66_out);
  LED led_25 (.in(_74typeflipflop_18_always));
  LED led_26 (.in(_74typeflipflop_18_always));
  LED led_27 (.in(_74typeflipflop_18_always));
  LED led_28 (.in(_74typeflipflop_18_always));
  LED led_29 (.in(_74typeflipflop_18_always));
  LED led_30 (.in(_74typeflipflop_18_always));
  LED led_31 (.in(_74typeflipflop_18_always));
  LED led_32 (.in(_74typeflipflop_18_always));
  LED led_33 (.in(_74typeflipflop_18_always));
  LED led_34 (.in(_74typeflipflop_18_always));
  LED led_35 (.in(_74typeflipflop_18_always));
  LED led_36 (.in(_74typeflipflop_18_always));
  LED led_37 (.in(_74typeflipflop_18_always));
  LED led_38 (.in(_74typeflipflop_18_always));
  LED led_39 (.in(_74typeflipflop_18_always));
  LED led_40 (.in(_74typeflipflop_18_always));
  _74TypeFlipFlop _74typeflipflop_20 (
    .CLK(and_43_out), .Data(pulldown_1_out[5]), .Load_A(dipswitch_3_out), .Load_B(dipswitch_4_out),
    .Always(_74typeflipflop_20_always), .Loaded_A(_74typeflipflop_25_loaded_a[5]),
    .Loaded_B(_74typeflipflop_25_loaded_b[5]), .Reset(reset_5_out));
  and and_68 (and_68_out, ARG2[0], not_20_out);
  and and_69 (and_69_out, and_73_out, not_19_out);
  and and_70 (and_70_out, and_68_out, not_19_out);
  and and_71 (and_87_out[4], not_27_out, and_69_out);
  and and_72 (and_87_out[5], not_27_out, and_70_out);
  LED led_41 (.in(_74typeflipflop_18_always));
  LED led_42 (.in(_74typeflipflop_18_always));
  LED led_43 (.in(_74typeflipflop_18_always));
  LED led_44 (.in(_74typeflipflop_18_always));
  LED led_45 (.in(_74typeflipflop_18_always));
  LED led_46 (.in(_74typeflipflop_18_always));
  LED led_47 (.in(_74typeflipflop_18_always));
  LED led_48 (.in(_74typeflipflop_18_always));
  LED led_49 (.in(_74typeflipflop_18_always));
  LED led_50 (.in(_74typeflipflop_18_always));
  LED led_51 (.in(_74typeflipflop_18_always));
  LED led_52 (.in(_74typeflipflop_18_always));
  LED led_53 (.in(_74typeflipflop_18_always));
  LED led_54 (.in(_74typeflipflop_18_always));
  LED led_55 (.in(_74typeflipflop_18_always));
  LED led_56 (.in(_74typeflipflop_18_always));
  and and_73 (and_73_out, not_21_out, not_20_out);
  LED led_57 (.in(_74typeflipflop_19_always));
  LED led_58 (.in(_74typeflipflop_19_always));
  LED led_59 (.in(_74typeflipflop_19_always));
  LED led_60 (.in(_74typeflipflop_19_always));
  LED led_61 (.in(_74typeflipflop_19_always));
  LED led_62 (.in(_74typeflipflop_19_always));
  LED led_63 (.in(_74typeflipflop_19_always));
  LED led_64 (.in(_74typeflipflop_19_always));
  _74TypeFlipFlop _74typeflipflop_21 (
    .CLK(and_43_out), .Data(pulldown_1_out[4]), .Load_A(dipswitch_3_out), .Load_B(dipswitch_4_out),
    .Always(_74typeflipflop_21_always), .Loaded_A(_74typeflipflop_25_loaded_a[4]),
    .Loaded_B(_74typeflipflop_25_loaded_b[4]), .Reset(reset_5_out));
  not not_20 (not_20_out, ARG2[1]);
  not not_21 (not_21_out, ARG2[0]);
  LED led_65 (.in(_74typeflipflop_19_always));
  LED led_66 (.in(_74typeflipflop_19_always));
  LED led_67 (.in(_74typeflipflop_19_always));
  LED led_68 (.in(_74typeflipflop_19_always));
  LED led_69 (.in(_74typeflipflop_19_always));
  LED led_70 (.in(_74typeflipflop_19_always));
  LED led_71 (.in(_74typeflipflop_19_always));
  LED led_72 (.in(_74typeflipflop_19_always));
  LED led_73 (.in(_74typeflipflop_19_always));
  LED led_74 (.in(_74typeflipflop_19_always));
  LED led_75 (.in(_74typeflipflop_19_always));
  LED led_76 (.in(_74typeflipflop_19_always));
  LED led_77 (.in(_74typeflipflop_19_always));
  LED led_78 (.in(_74typeflipflop_19_always));
  LED led_79 (.in(_74typeflipflop_19_always));
  LED led_80 (.in(_74typeflipflop_19_always));
  and and_74 (and_74_out, not_22_out, not_23_out);
  not not_22 (not_22_out, OPCODE[5]);
  not not_23 (not_23_out, OPCODE[4]);
  and and_75 (and_75_out, not_23_out, OPCODE[5]);
  // NotConnected on and_87_out[6]
  // NotConnected on and_87_out[7]
  LED led_81 (.in(_74typeflipflop_19_always));
  LED led_82 (.in(_74typeflipflop_19_always));
  LED led_83 (.in(_74typeflipflop_19_always));
  LED led_84 (.in(_74typeflipflop_19_always));
  LED led_85 (.in(_74typeflipflop_19_always));
  LED led_86 (.in(_74typeflipflop_19_always));
  LED led_87 (.in(_74typeflipflop_19_always));
  LED led_88 (.in(_74typeflipflop_19_always));
  LED led_89 (.in(_74typeflipflop_19_always));
  LED led_90 (.in(_74typeflipflop_19_always));
  LED led_91 (.in(_74typeflipflop_19_always));
  LED led_92 (.in(_74typeflipflop_19_always));
  LED led_93 (.in(_74typeflipflop_19_always));
  LED led_94 (.in(_74typeflipflop_19_always));
  LED led_95 (.in(_74typeflipflop_19_always));
  LED led_96 (.in(_74typeflipflop_19_always));
  not not_24 (not_24_out, ARG2[2]);
  and and_76 (and_76_out, and_79_out, not_24_out);
  and and_77 (and_87_out[3], not_27_out, and_76_out);
  LED led_97 (.in(_74typeflipflop_19_always));
  LED led_98 (.in(_74typeflipflop_19_always));
  LED led_99 (.in(_74typeflipflop_19_always));
  LED led_100 (.in(_74typeflipflop_19_always));
  LED led_101 (.in(_74typeflipflop_19_always));
  LED led_102 (.in(_74typeflipflop_19_always));
  LED led_103 (.in(_74typeflipflop_19_always));
  LED led_104 (.in(_74typeflipflop_19_always));
  LED led_105 (.in(_74typeflipflop_19_always));
  LED led_106 (.in(_74typeflipflop_19_always));
  LED led_107 (.in(_74typeflipflop_19_always));
  LED led_108 (.in(_74typeflipflop_19_always));
  LED led_109 (.in(_74typeflipflop_19_always));
  LED led_110 (.in(_74typeflipflop_19_always));
  LED led_111 (.in(_74typeflipflop_19_always));
  LED led_112 (.in(_74typeflipflop_19_always));
  _74TypeFlipFlop _74typeflipflop_22 (
    .CLK(and_43_out), .Data(pulldown_1_out[3]), .Load_A(dipswitch_3_out), .Load_B(dipswitch_4_out),
    .Always(_74typeflipflop_22_always), .Loaded_A(_74typeflipflop_25_loaded_a[3]),
    .Loaded_B(_74typeflipflop_25_loaded_b[3]), .Reset(reset_5_out));
  and and_78 (and_78_out, not_26_out, ARG2[1]);
  and and_79 (and_79_out, ARG2[1], ARG2[0]);
  and and_80 (and_80_out, and_78_out, not_24_out);
  and and_81 (and_87_out[2], not_27_out, and_80_out);
  LED led_113 (.in(_74typeflipflop_20_always));
  LED led_114 (.in(_74typeflipflop_20_always));
  LED led_115 (.in(_74typeflipflop_20_always));
  LED led_116 (.in(_74typeflipflop_20_always));
  LED led_117 (.in(_74typeflipflop_20_always));
  LED led_118 (.in(_74typeflipflop_20_always));
  LED led_119 (.in(_74typeflipflop_20_always));
  LED led_120 (.in(_74typeflipflop_20_always));
  and and_82 (and_82_out, ARG2[0], not_25_out);
  and and_83 (and_83_out, and_82_out, not_24_out);
  and and_84 (and_87_out[1], not_27_out, and_83_out);
  LED led_121 (.in(_74typeflipflop_20_always));
  LED led_122 (.in(_74typeflipflop_20_always));
  LED led_123 (.in(_74typeflipflop_20_always));
  LED led_124 (.in(_74typeflipflop_20_always));
  LED led_125 (.in(_74typeflipflop_20_always));
  LED led_126 (.in(_74typeflipflop_20_always));
  LED led_127 (.in(_74typeflipflop_20_always));
  LED led_128 (.in(_74typeflipflop_20_always));
  LED led_129 (.in(_74typeflipflop_20_always));
  LED led_130 (.in(_74typeflipflop_20_always));
  LED led_131 (.in(_74typeflipflop_20_always));
  LED led_132 (.in(_74typeflipflop_20_always));
  LED led_133 (.in(_74typeflipflop_20_always));
  LED led_134 (.in(_74typeflipflop_20_always));
  LED led_135 (.in(_74typeflipflop_20_always));
  LED led_136 (.in(_74typeflipflop_20_always));
  _74TypeFlipFlop _74typeflipflop_23 (
    .CLK(and_43_out), .Data(pulldown_1_out[2]), .Load_A(dipswitch_3_out), .Load_B(dipswitch_4_out),
    .Always(_74typeflipflop_23_always), .Loaded_A(_74typeflipflop_25_loaded_a[2]),
    .Loaded_B(_74typeflipflop_25_loaded_b[2]), .Reset(reset_5_out));
  and and_85 (and_85_out, not_26_out, not_25_out);
  and and_86 (and_86_out, and_85_out, not_24_out);
  and and_87 (and_87_out[0], not_27_out, and_86_out);
  LED led_137 (.in(_74typeflipflop_20_always));
  LED led_138 (.in(_74typeflipflop_20_always));
  LED led_139 (.in(_74typeflipflop_20_always));
  LED led_140 (.in(_74typeflipflop_20_always));
  LED led_141 (.in(_74typeflipflop_20_always));
  LED led_142 (.in(_74typeflipflop_20_always));
  LED led_143 (.in(_74typeflipflop_20_always));
  LED led_144 (.in(_74typeflipflop_20_always));
  LED led_145 (.in(_74typeflipflop_20_always));
  LED led_146 (.in(_74typeflipflop_20_always));
  LED led_147 (.in(_74typeflipflop_20_always));
  LED led_148 (.in(_74typeflipflop_20_always));
  LED led_149 (.in(_74typeflipflop_20_always));
  LED led_150 (.in(_74typeflipflop_20_always));
  LED led_151 (.in(_74typeflipflop_20_always));
  LED led_152 (.in(_74typeflipflop_20_always));
  not not_25 (not_25_out, ARG2[1]);
  not not_26 (not_26_out, ARG2[0]);
  not not_27 (not_27_out, or_14_out);
  LED led_153 (.in(_74typeflipflop_20_always));
  LED led_154 (.in(_74typeflipflop_20_always));
  LED led_155 (.in(_74typeflipflop_20_always));
  LED led_156 (.in(_74typeflipflop_20_always));
  LED led_157 (.in(_74typeflipflop_20_always));
  LED led_158 (.in(_74typeflipflop_20_always));
  LED led_159 (.in(_74typeflipflop_20_always));
  LED led_160 (.in(_74typeflipflop_20_always));
  LED led_161 (.in(_74typeflipflop_20_always));
  LED led_162 (.in(_74typeflipflop_20_always));
  LED led_163 (.in(_74typeflipflop_20_always));
  LED led_164 (.in(_74typeflipflop_20_always));
  LED led_165 (.in(_74typeflipflop_20_always));
  LED led_166 (.in(_74typeflipflop_20_always));
  LED led_167 (.in(_74typeflipflop_20_always));
  LED led_168 (.in(_74typeflipflop_20_always));
  LED led_169 (.in(_74typeflipflop_21_always));
  LED led_170 (.in(_74typeflipflop_21_always));
  LED led_171 (.in(_74typeflipflop_21_always));
  LED led_172 (.in(_74typeflipflop_21_always));
  LED led_173 (.in(_74typeflipflop_21_always));
  LED led_174 (.in(_74typeflipflop_21_always));
  LED led_175 (.in(_74typeflipflop_21_always));
  LED led_176 (.in(_74typeflipflop_21_always));
  _74TypeFlipFlop _74typeflipflop_24 (
    .CLK(and_43_out), .Data(pulldown_1_out[1]), .Load_A(dipswitch_3_out), .Load_B(dipswitch_4_out),
    .Always(_74typeflipflop_24_always), .Loaded_A(_74typeflipflop_25_loaded_a[1]),
    .Loaded_B(_74typeflipflop_25_loaded_b[1]), .Reset(reset_5_out));
  or or_14 (or_14_out, and_37_out, OPCODE[6]);
  LED led_177 (.in(_74typeflipflop_21_always));
  LED led_178 (.in(_74typeflipflop_21_always));
  LED led_179 (.in(_74typeflipflop_21_always));
  LED led_180 (.in(_74typeflipflop_21_always));
  LED led_181 (.in(_74typeflipflop_21_always));
  LED led_182 (.in(_74typeflipflop_21_always));
  LED led_183 (.in(_74typeflipflop_21_always));
  LED led_184 (.in(_74typeflipflop_21_always));
  LED led_185 (.in(_74typeflipflop_21_always));
  LED led_186 (.in(_74typeflipflop_21_always));
  LED led_187 (.in(_74typeflipflop_21_always));
  LED led_188 (.in(_74typeflipflop_21_always));
  LED led_189 (.in(_74typeflipflop_21_always));
  LED led_190 (.in(_74typeflipflop_21_always));
  LED led_191 (.in(_74typeflipflop_21_always));
  LED led_192 (.in(_74typeflipflop_21_always));
  LED led_193 (.in(_74typeflipflop_21_always));
  LED led_194 (.in(_74typeflipflop_21_always));
  LED led_195 (.in(_74typeflipflop_21_always));
  LED led_196 (.in(_74typeflipflop_21_always));
  LED led_197 (.in(_74typeflipflop_21_always));
  LED led_198 (.in(_74typeflipflop_21_always));
  LED led_199 (.in(_74typeflipflop_21_always));
  LED led_200 (.in(_74typeflipflop_21_always));
  LED led_201 (.in(_74typeflipflop_21_always));
  LED led_202 (.in(_74typeflipflop_21_always));
  LED led_203 (.in(_74typeflipflop_21_always));
  LED led_204 (.in(_74typeflipflop_21_always));
  LED led_205 (.in(_74typeflipflop_21_always));
  LED led_206 (.in(_74typeflipflop_21_always));
  LED led_207 (.in(_74typeflipflop_21_always));
  LED led_208 (.in(_74typeflipflop_21_always));
  _74TypeFlipFlop _74typeflipflop_25 (
    .CLK(and_43_out), .Data(pulldown_1_out[0]), .Load_A(dipswitch_3_out), .Load_B(dipswitch_4_out),
    .Always(_74typeflipflop_25_always), .Loaded_A(_74typeflipflop_25_loaded_a[0]),
    .Loaded_B(_74typeflipflop_25_loaded_b[0]), .Reset(reset_5_out));
  LED led_209 (.in(_74typeflipflop_21_always));
  LED led_210 (.in(_74typeflipflop_21_always));
  LED led_211 (.in(_74typeflipflop_21_always));
  LED led_212 (.in(_74typeflipflop_21_always));
  LED led_213 (.in(_74typeflipflop_21_always));
  LED led_214 (.in(_74typeflipflop_21_always));
  LED led_215 (.in(_74typeflipflop_21_always));
  LED led_216 (.in(_74typeflipflop_21_always));
  LED led_217 (.in(_74typeflipflop_21_always));
  LED led_218 (.in(_74typeflipflop_21_always));
  LED led_219 (.in(_74typeflipflop_21_always));
  LED led_220 (.in(_74typeflipflop_21_always));
  LED led_221 (.in(_74typeflipflop_21_always));
  LED led_222 (.in(_74typeflipflop_21_always));
  LED led_223 (.in(_74typeflipflop_21_always));
  LED led_224 (.in(_74typeflipflop_21_always));
  DipSwitch dipswitch_3 (.out(dipswitch_3_out));
  not not_28 (not_28_out, ARG1[2]);
  not not_29 (not_29_out, not_28_out);
  and and_88 (and_88_out, and_91_out, not_29_out);
  and and_89 (and_89_out, not_35_out, and_88_out);
  LED led_225 (.in(_74typeflipflop_22_always));
  LED led_226 (.in(_74typeflipflop_22_always));
  LED led_227 (.in(_74typeflipflop_22_always));
  LED led_228 (.in(_74typeflipflop_22_always));
  LED led_229 (.in(_74typeflipflop_22_always));
  LED led_230 (.in(_74typeflipflop_22_always));
  LED led_231 (.in(_74typeflipflop_22_always));
  LED led_232 (.in(_74typeflipflop_22_always));
  Reset #(.invertOutput("false")) reset_5 (.out(reset_5_out));
  DipSwitch dipswitch_4 (.out(dipswitch_4_out));
  and and_90 (and_90_out, not_31_out, ARG1[1]);
  and and_91 (and_91_out, ARG1[1], ARG1[0]);
  and and_92 (and_92_out, and_90_out, not_29_out);
  and and_93 (and_93_out, not_35_out, and_92_out);
  LED led_233 (.in(_74typeflipflop_22_always));
  LED led_234 (.in(_74typeflipflop_22_always));
  LED led_235 (.in(_74typeflipflop_22_always));
  LED led_236 (.in(_74typeflipflop_22_always));
  LED led_237 (.in(_74typeflipflop_22_always));
  LED led_238 (.in(_74typeflipflop_22_always));
  LED led_239 (.in(_74typeflipflop_22_always));
  LED led_240 (.in(_74typeflipflop_22_always));
  LED led_241 (.in(_74typeflipflop_22_always));
  LED led_242 (.in(_74typeflipflop_22_always));
  LED led_243 (.in(_74typeflipflop_22_always));
  LED led_244 (.in(_74typeflipflop_22_always));
  LED led_245 (.in(_74typeflipflop_22_always));
  LED led_246 (.in(_74typeflipflop_22_always));
  LED led_247 (.in(_74typeflipflop_22_always));
  LED led_248 (.in(_74typeflipflop_22_always));
  and and_94 (and_94_out, ARG1[0], not_30_out);
  and and_95 (and_95_out, and_94_out, not_29_out);
  and and_96 (and_111_out[5], not_35_out, and_95_out);
  LED led_249 (.in(_74typeflipflop_22_always));
  LED led_250 (.in(_74typeflipflop_22_always));
  LED led_251 (.in(_74typeflipflop_22_always));
  LED led_252 (.in(_74typeflipflop_22_always));
  LED led_253 (.in(_74typeflipflop_22_always));
  LED led_254 (.in(_74typeflipflop_22_always));
  LED led_255 (.in(_74typeflipflop_22_always));
  LED led_256 (.in(_74typeflipflop_22_always));
  LED led_257 (.in(_74typeflipflop_22_always));
  LED led_258 (.in(_74typeflipflop_22_always));
  LED led_259 (.in(_74typeflipflop_22_always));
  LED led_260 (.in(_74typeflipflop_22_always));
  LED led_261 (.in(_74typeflipflop_22_always));
  LED led_262 (.in(_74typeflipflop_22_always));
  LED led_263 (.in(_74typeflipflop_22_always));
  LED led_264 (.in(_74typeflipflop_22_always));
  and and_97 (and_97_out, not_31_out, not_30_out);
  and and_98 (and_98_out, and_97_out, not_29_out);
  and and_99 (and_111_out[4], not_35_out, and_98_out);
  LED led_265 (.in(_74typeflipflop_22_always));
  LED led_266 (.in(_74typeflipflop_22_always));
  LED led_267 (.in(_74typeflipflop_22_always));
  LED led_268 (.in(_74typeflipflop_22_always));
  LED led_269 (.in(_74typeflipflop_22_always));
  LED led_270 (.in(_74typeflipflop_22_always));
  LED led_271 (.in(_74typeflipflop_22_always));
  LED led_272 (.in(_74typeflipflop_22_always));
  LED led_273 (.in(_74typeflipflop_22_always));
  LED led_274 (.in(_74typeflipflop_22_always));
  LED led_275 (.in(_74typeflipflop_22_always));
  LED led_276 (.in(_74typeflipflop_22_always));
  LED led_277 (.in(_74typeflipflop_22_always));
  LED led_278 (.in(_74typeflipflop_22_always));
  LED led_279 (.in(_74typeflipflop_22_always));
  LED led_280 (.in(_74typeflipflop_22_always));
  not not_30 (not_30_out, ARG1[1]);
  not not_31 (not_31_out, ARG1[0]);
  LED led_281 (.in(_74typeflipflop_23_always));
  LED led_282 (.in(_74typeflipflop_23_always));
  LED led_283 (.in(_74typeflipflop_23_always));
  LED led_284 (.in(_74typeflipflop_23_always));
  LED led_285 (.in(_74typeflipflop_23_always));
  LED led_286 (.in(_74typeflipflop_23_always));
  LED led_287 (.in(_74typeflipflop_23_always));
  LED led_288 (.in(_74typeflipflop_23_always));
  // NotConnected on and_111_out[6]
  // NotConnected on and_111_out[7]
  LED led_289 (.in(_74typeflipflop_23_always));
  LED led_290 (.in(_74typeflipflop_23_always));
  LED led_291 (.in(_74typeflipflop_23_always));
  LED led_292 (.in(_74typeflipflop_23_always));
  LED led_293 (.in(_74typeflipflop_23_always));
  LED led_294 (.in(_74typeflipflop_23_always));
  LED led_295 (.in(_74typeflipflop_23_always));
  LED led_296 (.in(_74typeflipflop_23_always));
  LED led_297 (.in(_74typeflipflop_23_always));
  LED led_298 (.in(_74typeflipflop_23_always));
  LED led_299 (.in(_74typeflipflop_23_always));
  LED led_300 (.in(_74typeflipflop_23_always));
  LED led_301 (.in(_74typeflipflop_23_always));
  LED led_302 (.in(_74typeflipflop_23_always));
  LED led_303 (.in(_74typeflipflop_23_always));
  LED led_304 (.in(_74typeflipflop_23_always));
  not not_32 (not_32_out, ARG1[2]);
  LED led_305 (.in(_74typeflipflop_23_always));
  LED led_306 (.in(_74typeflipflop_23_always));
  LED led_307 (.in(_74typeflipflop_23_always));
  LED led_308 (.in(_74typeflipflop_23_always));
  LED led_309 (.in(_74typeflipflop_23_always));
  LED led_310 (.in(_74typeflipflop_23_always));
  LED led_311 (.in(_74typeflipflop_23_always));
  LED led_312 (.in(_74typeflipflop_23_always));
  LED led_313 (.in(_74typeflipflop_23_always));
  LED led_314 (.in(_74typeflipflop_23_always));
  LED led_315 (.in(_74typeflipflop_23_always));
  LED led_316 (.in(_74typeflipflop_23_always));
  LED led_317 (.in(_74typeflipflop_23_always));
  LED led_318 (.in(_74typeflipflop_23_always));
  LED led_319 (.in(_74typeflipflop_23_always));
  LED led_320 (.in(_74typeflipflop_23_always));
  and and_100 (and_100_out, ARG1[1], ARG1[0]);
  and and_101 (and_101_out, and_106_out, not_32_out);
  and and_102 (and_102_out, and_100_out, not_32_out);
  and and_103 (and_111_out[2], not_35_out, and_101_out);
  and and_104 (and_111_out[3], not_35_out, and_102_out);
  LED led_321 (.in(_74typeflipflop_23_always));
  LED led_322 (.in(_74typeflipflop_23_always));
  LED led_323 (.in(_74typeflipflop_23_always));
  LED led_324 (.in(_74typeflipflop_23_always));
  LED led_325 (.in(_74typeflipflop_23_always));
  LED led_326 (.in(_74typeflipflop_23_always));
  LED led_327 (.in(_74typeflipflop_23_always));
  LED led_328 (.in(_74typeflipflop_23_always));
  LED led_329 (.in(_74typeflipflop_23_always));
  LED led_330 (.in(_74typeflipflop_23_always));
  LED led_331 (.in(_74typeflipflop_23_always));
  LED led_332 (.in(_74typeflipflop_23_always));
  LED led_333 (.in(_74typeflipflop_23_always));
  LED led_334 (.in(_74typeflipflop_23_always));
  LED led_335 (.in(_74typeflipflop_23_always));
  LED led_336 (.in(_74typeflipflop_23_always));
  and and_105 (and_105_out, ARG1[0], not_33_out);
  and and_106 (and_106_out, not_34_out, ARG1[1]);
  and and_107 (and_107_out, and_105_out, not_32_out);
  and and_108 (and_111_out[1], not_35_out, and_107_out);
  LED led_337 (.in(_74typeflipflop_24_always));
  LED led_338 (.in(_74typeflipflop_24_always));
  LED led_339 (.in(_74typeflipflop_24_always));
  LED led_340 (.in(_74typeflipflop_24_always));
  LED led_341 (.in(_74typeflipflop_24_always));
  LED led_342 (.in(_74typeflipflop_24_always));
  LED led_343 (.in(_74typeflipflop_24_always));
  LED led_344 (.in(_74typeflipflop_24_always));
  and and_109 (and_109_out, not_34_out, not_33_out);
  and and_110 (and_110_out, and_109_out, not_32_out);
  and and_111 (and_111_out[0], not_35_out, and_110_out);
  LED led_345 (.in(_74typeflipflop_24_always));
  LED led_346 (.in(_74typeflipflop_24_always));
  LED led_347 (.in(_74typeflipflop_24_always));
  LED led_348 (.in(_74typeflipflop_24_always));
  LED led_349 (.in(_74typeflipflop_24_always));
  LED led_350 (.in(_74typeflipflop_24_always));
  LED led_351 (.in(_74typeflipflop_24_always));
  LED led_352 (.in(_74typeflipflop_24_always));
  LED led_353 (.in(_74typeflipflop_24_always));
  LED led_354 (.in(_74typeflipflop_24_always));
  LED led_355 (.in(_74typeflipflop_24_always));
  LED led_356 (.in(_74typeflipflop_24_always));
  LED led_357 (.in(_74typeflipflop_24_always));
  LED led_358 (.in(_74typeflipflop_24_always));
  LED led_359 (.in(_74typeflipflop_24_always));
  LED led_360 (.in(_74typeflipflop_24_always));
  not not_33 (not_33_out, ARG1[1]);
  not not_34 (not_34_out, ARG1[0]);
  not not_35 (not_35_out, or_15_out);
  LED led_361 (.in(_74typeflipflop_24_always));
  LED led_362 (.in(_74typeflipflop_24_always));
  LED led_363 (.in(_74typeflipflop_24_always));
  LED led_364 (.in(_74typeflipflop_24_always));
  LED led_365 (.in(_74typeflipflop_24_always));
  LED led_366 (.in(_74typeflipflop_24_always));
  LED led_367 (.in(_74typeflipflop_24_always));
  LED led_368 (.in(_74typeflipflop_24_always));
  LED led_369 (.in(_74typeflipflop_24_always));
  LED led_370 (.in(_74typeflipflop_24_always));
  LED led_371 (.in(_74typeflipflop_24_always));
  LED led_372 (.in(_74typeflipflop_24_always));
  LED led_373 (.in(_74typeflipflop_24_always));
  LED led_374 (.in(_74typeflipflop_24_always));
  LED led_375 (.in(_74typeflipflop_24_always));
  LED led_376 (.in(_74typeflipflop_24_always));
  LED led_377 (.in(_74typeflipflop_24_always));
  LED led_378 (.in(_74typeflipflop_24_always));
  LED led_379 (.in(_74typeflipflop_24_always));
  LED led_380 (.in(_74typeflipflop_24_always));
  LED led_381 (.in(_74typeflipflop_24_always));
  LED led_382 (.in(_74typeflipflop_24_always));
  LED led_383 (.in(_74typeflipflop_24_always));
  LED led_384 (.in(_74typeflipflop_24_always));
  LED led_385 (.in(_74typeflipflop_24_always));
  LED led_386 (.in(_74typeflipflop_24_always));
  LED led_387 (.in(_74typeflipflop_24_always));
  LED led_388 (.in(_74typeflipflop_24_always));
  LED led_389 (.in(_74typeflipflop_24_always));
  LED led_390 (.in(_74typeflipflop_24_always));
  LED led_391 (.in(_74typeflipflop_24_always));
  LED led_392 (.in(_74typeflipflop_24_always));
  LED led_393 (.in(_74typeflipflop_25_always));
  LED led_394 (.in(_74typeflipflop_25_always));
  LED led_395 (.in(_74typeflipflop_25_always));
  LED led_396 (.in(_74typeflipflop_25_always));
  LED led_397 (.in(_74typeflipflop_25_always));
  LED led_398 (.in(_74typeflipflop_25_always));
  LED led_399 (.in(_74typeflipflop_25_always));
  LED led_400 (.in(_74typeflipflop_25_always));
  LED led_401 (.in(_74typeflipflop_25_always));
  LED led_402 (.in(_74typeflipflop_25_always));
  LED led_403 (.in(_74typeflipflop_25_always));
  LED led_404 (.in(_74typeflipflop_25_always));
  LED led_405 (.in(_74typeflipflop_25_always));
  LED led_406 (.in(_74typeflipflop_25_always));
  LED led_407 (.in(_74typeflipflop_25_always));
  LED led_408 (.in(_74typeflipflop_25_always));
  LED led_409 (.in(_74typeflipflop_25_always));
  LED led_410 (.in(_74typeflipflop_25_always));
  LED led_411 (.in(_74typeflipflop_25_always));
  LED led_412 (.in(_74typeflipflop_25_always));
  LED led_413 (.in(_74typeflipflop_25_always));
  LED led_414 (.in(_74typeflipflop_25_always));
  LED led_415 (.in(_74typeflipflop_25_always));
  LED led_416 (.in(_74typeflipflop_25_always));
  or or_15 (or_15_out, and_27_out, OPCODE[7]);
  LED led_417 (.in(_74typeflipflop_25_always));
  LED led_418 (.in(_74typeflipflop_25_always));
  LED led_419 (.in(_74typeflipflop_25_always));
  LED led_420 (.in(_74typeflipflop_25_always));
  LED led_421 (.in(_74typeflipflop_25_always));
  LED led_422 (.in(_74typeflipflop_25_always));
  LED led_423 (.in(_74typeflipflop_25_always));
  LED led_424 (.in(_74typeflipflop_25_always));
  LED led_425 (.in(_74typeflipflop_25_always));
  LED led_426 (.in(_74typeflipflop_25_always));
  LED led_427 (.in(_74typeflipflop_25_always));
  LED led_428 (.in(_74typeflipflop_25_always));
  LED led_429 (.in(_74typeflipflop_25_always));
  LED led_430 (.in(_74typeflipflop_25_always));
  LED led_431 (.in(_74typeflipflop_25_always));
  LED led_432 (.in(_74typeflipflop_25_always));
  LED led_433 (.in(_74typeflipflop_25_always));
  LED led_434 (.in(_74typeflipflop_25_always));
  LED led_435 (.in(_74typeflipflop_25_always));
  LED led_436 (.in(_74typeflipflop_25_always));
  LED led_437 (.in(_74typeflipflop_25_always));
  LED led_438 (.in(_74typeflipflop_25_always));
  LED led_439 (.in(_74typeflipflop_25_always));
  LED led_440 (.in(_74typeflipflop_25_always));
  LED led_441 (.in(_74typeflipflop_25_always));
  LED led_442 (.in(_74typeflipflop_25_always));
  LED led_443 (.in(_74typeflipflop_25_always));
  LED led_444 (.in(_74typeflipflop_25_always));
  LED led_445 (.in(_74typeflipflop_25_always));
  LED led_446 (.in(_74typeflipflop_25_always));
  LED led_447 (.in(_74typeflipflop_25_always));
  LED led_448 (.in(_74typeflipflop_25_always));
  Reset #(.invertOutput("false")) reset_6 (.out(reset_6_out));
  Reset #(.invertOutput("false")) reset_7 (.out(reset_7_out));
  Reset #(.invertOutput("false")) reset_8 (.out(reset_8_out));
  Reset #(.invertOutput("false")) reset_9 (.out(reset_9_out));
  Reset #(.invertOutput("false")) reset_10 (.out(reset_10_out));
  Reset #(.invertOutput("false")) reset_11 (.out(reset_11_out));
  // NotConnected on notconnected_5_out
  ROM #(.AddrBits(8), .Bits(8)) rom_1 (.A(notconnected_5_out), .sel(1'b1), .D(rom_1_d));
  _74TypeFlipFlop _74typeflipflop_26 (
    .CLK(_74typeflipflop_16_loaded_a[0]), .Data(_74typeflipflop_8_loaded_a[7]), .Load_A(and_111_out[0]),
    .Load_B(and_87_out[0]), .Always(_74typeflipflop_26_always), .Loaded_A(driver_33_out[7]),
    .Loaded_B(driver_48_out[7]), .Reset(reset_6_out));
  _74TypeFlipFlop _74typeflipflop_27 (
    .CLK(_74typeflipflop_16_loaded_a[0]), .Data(_74typeflipflop_8_loaded_a[6]), .Load_A(and_111_out[0]),
    .Load_B(and_87_out[0]), .Always(_74typeflipflop_27_always), .Loaded_A(driver_33_out[6]),
    .Loaded_B(driver_48_out[6]), .Reset(reset_6_out));
  _74TypeFlipFlop _74typeflipflop_28 (
    .CLK(_74typeflipflop_16_loaded_a[0]), .Data(_74typeflipflop_8_loaded_a[5]), .Load_A(and_111_out[0]),
    .Load_B(and_87_out[0]), .Always(_74typeflipflop_28_always), .Loaded_A(driver_33_out[5]),
    .Loaded_B(driver_48_out[5]), .Reset(reset_6_out));
  _74TypeFlipFlop _74typeflipflop_29 (
    .CLK(_74typeflipflop_16_loaded_a[0]), .Data(_74typeflipflop_8_loaded_a[4]), .Load_A(and_111_out[0]),
    .Load_B(and_87_out[0]), .Always(_74typeflipflop_29_always), .Loaded_A(driver_33_out[4]),
    .Loaded_B(driver_48_out[4]), .Reset(reset_6_out));
  _74TypeFlipFlop _74typeflipflop_30 (
    .CLK(_74typeflipflop_16_loaded_a[0]), .Data(_74typeflipflop_8_loaded_a[3]), .Load_A(and_111_out[0]),
    .Load_B(and_87_out[0]), .Always(_74typeflipflop_30_always), .Loaded_A(driver_33_out[3]),
    .Loaded_B(driver_48_out[3]), .Reset(reset_6_out));
  _74TypeFlipFlop _74typeflipflop_31 (
    .CLK(_74typeflipflop_16_loaded_a[0]), .Data(_74typeflipflop_8_loaded_a[2]), .Load_A(and_111_out[0]),
    .Load_B(and_87_out[0]), .Always(_74typeflipflop_31_always), .Loaded_A(driver_33_out[2]),
    .Loaded_B(driver_48_out[2]), .Reset(reset_6_out));
  _74TypeFlipFlop _74typeflipflop_32 (
    .CLK(_74typeflipflop_16_loaded_a[0]), .Data(_74typeflipflop_8_loaded_a[1]), .Load_A(and_111_out[0]),
    .Load_B(and_87_out[0]), .Always(_74typeflipflop_32_always), .Loaded_A(driver_33_out[1]),
    .Loaded_B(driver_48_out[1]), .Reset(reset_6_out));
  _74TypeFlipFlop _74typeflipflop_33 (
    .CLK(_74typeflipflop_16_loaded_a[0]), .Data(_74typeflipflop_8_loaded_a[0]), .Load_A(and_111_out[0]),
    .Load_B(and_87_out[0]), .Always(_74typeflipflop_33_always), .Loaded_A(driver_33_out[0]),
    .Loaded_B(driver_48_out[0]), .Reset(reset_6_out));
  _74TypeFlipFlop _74typeflipflop_34 (
    .CLK(_74typeflipflop_16_loaded_a[1]), .Data(_74typeflipflop_8_loaded_a[7]), .Load_A(and_111_out[1]),
    .Load_B(and_87_out[1]), .Always(_74typeflipflop_41_always[7]), .Loaded_A(driver_33_out[7]),
    .Loaded_B(driver_48_out[7]), .Reset(reset_7_out));
  _74TypeFlipFlop _74typeflipflop_35 (
    .CLK(_74typeflipflop_16_loaded_a[1]), .Data(_74typeflipflop_8_loaded_a[6]), .Load_A(and_111_out[1]),
    .Load_B(and_87_out[1]), .Always(_74typeflipflop_41_always[6]), .Loaded_A(driver_33_out[6]),
    .Loaded_B(driver_48_out[6]), .Reset(reset_7_out));
  _74TypeFlipFlop _74typeflipflop_36 (
    .CLK(_74typeflipflop_16_loaded_a[1]), .Data(_74typeflipflop_8_loaded_a[5]), .Load_A(and_111_out[1]),
    .Load_B(and_87_out[1]), .Always(_74typeflipflop_41_always[5]), .Loaded_A(driver_33_out[5]),
    .Loaded_B(driver_48_out[5]), .Reset(reset_7_out));
  _74TypeFlipFlop _74typeflipflop_37 (
    .CLK(_74typeflipflop_16_loaded_a[1]), .Data(_74typeflipflop_8_loaded_a[4]), .Load_A(and_111_out[1]),
    .Load_B(and_87_out[1]), .Always(_74typeflipflop_41_always[4]), .Loaded_A(driver_33_out[4]),
    .Loaded_B(driver_48_out[4]), .Reset(reset_7_out));
  _74TypeFlipFlop _74typeflipflop_38 (
    .CLK(_74typeflipflop_16_loaded_a[1]), .Data(_74typeflipflop_8_loaded_a[3]), .Load_A(and_111_out[1]),
    .Load_B(and_87_out[1]), .Always(_74typeflipflop_41_always[3]), .Loaded_A(driver_33_out[3]),
    .Loaded_B(driver_48_out[3]), .Reset(reset_7_out));
  _74TypeFlipFlop _74typeflipflop_39 (
    .CLK(_74typeflipflop_16_loaded_a[1]), .Data(_74typeflipflop_8_loaded_a[2]), .Load_A(and_111_out[1]),
    .Load_B(and_87_out[1]), .Always(_74typeflipflop_41_always[2]), .Loaded_A(driver_33_out[2]),
    .Loaded_B(driver_48_out[2]), .Reset(reset_7_out));
  _74TypeFlipFlop _74typeflipflop_40 (
    .CLK(_74typeflipflop_16_loaded_a[1]), .Data(_74typeflipflop_8_loaded_a[1]), .Load_A(and_111_out[1]),
    .Load_B(and_87_out[1]), .Always(_74typeflipflop_41_always[1]), .Loaded_A(driver_33_out[1]),
    .Loaded_B(driver_48_out[1]), .Reset(reset_7_out));
  _74TypeFlipFlop _74typeflipflop_41 (
    .CLK(_74typeflipflop_16_loaded_a[1]), .Data(_74typeflipflop_8_loaded_a[0]), .Load_A(and_111_out[1]),
    .Load_B(and_87_out[1]), .Always(_74typeflipflop_41_always[0]), .Loaded_A(driver_33_out[0]),
    .Loaded_B(driver_48_out[0]), .Reset(reset_7_out));
  _74TypeFlipFlop _74typeflipflop_42 (
    .CLK(_74typeflipflop_16_loaded_a[2]), .Data(_74typeflipflop_8_loaded_a[7]), .Load_A(and_111_out[2]),
    .Load_B(and_87_out[2]), .Always(_74typeflipflop_42_always), .Loaded_A(driver_33_out[7]),
    .Loaded_B(driver_48_out[7]), .Reset(reset_8_out));
  _74TypeFlipFlop _74typeflipflop_43 (
    .CLK(_74typeflipflop_16_loaded_a[2]), .Data(_74typeflipflop_8_loaded_a[6]), .Load_A(and_111_out[2]),
    .Load_B(and_87_out[2]), .Always(_74typeflipflop_43_always), .Loaded_A(driver_33_out[6]),
    .Loaded_B(driver_48_out[6]), .Reset(reset_8_out));
  _74TypeFlipFlop _74typeflipflop_44 (
    .CLK(_74typeflipflop_16_loaded_a[2]), .Data(_74typeflipflop_8_loaded_a[5]), .Load_A(and_111_out[2]),
    .Load_B(and_87_out[2]), .Always(_74typeflipflop_44_always), .Loaded_A(driver_33_out[5]),
    .Loaded_B(driver_48_out[5]), .Reset(reset_8_out));
  _74TypeFlipFlop _74typeflipflop_45 (
    .CLK(_74typeflipflop_16_loaded_a[2]), .Data(_74typeflipflop_8_loaded_a[4]), .Load_A(and_111_out[2]),
    .Load_B(and_87_out[2]), .Always(_74typeflipflop_45_always), .Loaded_A(driver_33_out[4]),
    .Loaded_B(driver_48_out[4]), .Reset(reset_8_out));
  _74TypeFlipFlop _74typeflipflop_46 (
    .CLK(_74typeflipflop_16_loaded_a[2]), .Data(_74typeflipflop_8_loaded_a[3]), .Load_A(and_111_out[2]),
    .Load_B(and_87_out[2]), .Always(_74typeflipflop_46_always), .Loaded_A(driver_33_out[3]),
    .Loaded_B(driver_48_out[3]), .Reset(reset_8_out));
  _74TypeFlipFlop _74typeflipflop_47 (
    .CLK(_74typeflipflop_16_loaded_a[2]), .Data(_74typeflipflop_8_loaded_a[2]), .Load_A(and_111_out[2]),
    .Load_B(and_87_out[2]), .Always(_74typeflipflop_47_always), .Loaded_A(driver_33_out[2]),
    .Loaded_B(driver_48_out[2]), .Reset(reset_8_out));
  _74TypeFlipFlop _74typeflipflop_48 (
    .CLK(_74typeflipflop_16_loaded_a[2]), .Data(_74typeflipflop_8_loaded_a[1]), .Load_A(and_111_out[2]),
    .Load_B(and_87_out[2]), .Always(_74typeflipflop_48_always), .Loaded_A(driver_33_out[1]),
    .Loaded_B(driver_48_out[1]), .Reset(reset_8_out));
  _74TypeFlipFlop _74typeflipflop_49 (
    .CLK(_74typeflipflop_16_loaded_a[2]), .Data(_74typeflipflop_8_loaded_a[0]), .Load_A(and_111_out[2]),
    .Load_B(and_87_out[2]), .Always(_74typeflipflop_49_always), .Loaded_A(driver_33_out[0]),
    .Loaded_B(driver_48_out[0]), .Reset(reset_8_out));
  _74TypeFlipFlop _74typeflipflop_50 (
    .CLK(_74typeflipflop_16_loaded_a[3]), .Data(_74typeflipflop_8_loaded_a[7]), .Load_A(and_111_out[3]),
    .Load_B(and_87_out[3]), .Always(_74typeflipflop_50_always), .Loaded_A(driver_33_out[7]),
    .Loaded_B(driver_48_out[7]), .Reset(reset_9_out));
  _74TypeFlipFlop _74typeflipflop_51 (
    .CLK(_74typeflipflop_16_loaded_a[3]), .Data(_74typeflipflop_8_loaded_a[6]), .Load_A(and_111_out[3]),
    .Load_B(and_87_out[3]), .Always(_74typeflipflop_51_always), .Loaded_A(driver_33_out[6]),
    .Loaded_B(driver_48_out[6]), .Reset(reset_9_out));
  _74TypeFlipFlop _74typeflipflop_52 (
    .CLK(_74typeflipflop_16_loaded_a[3]), .Data(_74typeflipflop_8_loaded_a[5]), .Load_A(and_111_out[3]),
    .Load_B(and_87_out[3]), .Always(_74typeflipflop_52_always), .Loaded_A(driver_33_out[5]),
    .Loaded_B(driver_48_out[5]), .Reset(reset_9_out));
  _74TypeFlipFlop _74typeflipflop_53 (
    .CLK(_74typeflipflop_16_loaded_a[3]), .Data(_74typeflipflop_8_loaded_a[4]), .Load_A(and_111_out[3]),
    .Load_B(and_87_out[3]), .Always(_74typeflipflop_53_always), .Loaded_A(driver_33_out[4]),
    .Loaded_B(driver_48_out[4]), .Reset(reset_9_out));
  _74TypeFlipFlop _74typeflipflop_54 (
    .CLK(_74typeflipflop_16_loaded_a[3]), .Data(_74typeflipflop_8_loaded_a[3]), .Load_A(and_111_out[3]),
    .Load_B(and_87_out[3]), .Always(_74typeflipflop_54_always), .Loaded_A(driver_33_out[3]),
    .Loaded_B(driver_48_out[3]), .Reset(reset_9_out));
  _74TypeFlipFlop _74typeflipflop_55 (
    .CLK(_74typeflipflop_16_loaded_a[3]), .Data(_74typeflipflop_8_loaded_a[2]), .Load_A(and_111_out[3]),
    .Load_B(and_87_out[3]), .Always(_74typeflipflop_55_always), .Loaded_A(driver_33_out[2]),
    .Loaded_B(driver_48_out[2]), .Reset(reset_9_out));
  _74TypeFlipFlop _74typeflipflop_56 (
    .CLK(_74typeflipflop_16_loaded_a[3]), .Data(_74typeflipflop_8_loaded_a[1]), .Load_A(and_111_out[3]),
    .Load_B(and_87_out[3]), .Always(_74typeflipflop_56_always), .Loaded_A(driver_33_out[1]),
    .Loaded_B(driver_48_out[1]), .Reset(reset_9_out));
  _74TypeFlipFlop _74typeflipflop_57 (
    .CLK(_74typeflipflop_16_loaded_a[3]), .Data(_74typeflipflop_8_loaded_a[0]), .Load_A(and_111_out[3]),
    .Load_B(and_87_out[3]), .Always(_74typeflipflop_57_always), .Loaded_A(driver_33_out[0]),
    .Loaded_B(driver_48_out[0]), .Reset(reset_9_out));
  _74TypeFlipFlop _74typeflipflop_58 (
    .CLK(_74typeflipflop_16_loaded_a[4]), .Data(_74typeflipflop_8_loaded_a[7]), .Load_A(and_111_out[4]),
    .Load_B(and_87_out[4]), .Always(_74typeflipflop_58_always), .Loaded_A(driver_33_out[7]),
    .Loaded_B(driver_48_out[7]), .Reset(reset_10_out));
  _74TypeFlipFlop _74typeflipflop_59 (
    .CLK(_74typeflipflop_16_loaded_a[4]), .Data(_74typeflipflop_8_loaded_a[6]), .Load_A(and_111_out[4]),
    .Load_B(and_87_out[4]), .Always(_74typeflipflop_59_always), .Loaded_A(driver_33_out[6]),
    .Loaded_B(driver_48_out[6]), .Reset(reset_10_out));
  _74TypeFlipFlop _74typeflipflop_60 (
    .CLK(_74typeflipflop_16_loaded_a[4]), .Data(_74typeflipflop_8_loaded_a[5]), .Load_A(and_111_out[4]),
    .Load_B(and_87_out[4]), .Always(_74typeflipflop_60_always), .Loaded_A(driver_33_out[5]),
    .Loaded_B(driver_48_out[5]), .Reset(reset_10_out));
  _74TypeFlipFlop _74typeflipflop_61 (
    .CLK(_74typeflipflop_16_loaded_a[4]), .Data(_74typeflipflop_8_loaded_a[4]), .Load_A(and_111_out[4]),
    .Load_B(and_87_out[4]), .Always(_74typeflipflop_61_always), .Loaded_A(driver_33_out[4]),
    .Loaded_B(driver_48_out[4]), .Reset(reset_10_out));
  _74TypeFlipFlop _74typeflipflop_62 (
    .CLK(_74typeflipflop_16_loaded_a[4]), .Data(_74typeflipflop_8_loaded_a[3]), .Load_A(and_111_out[4]),
    .Load_B(and_87_out[4]), .Always(_74typeflipflop_62_always), .Loaded_A(driver_33_out[3]),
    .Loaded_B(driver_48_out[3]), .Reset(reset_10_out));
  _74TypeFlipFlop _74typeflipflop_63 (
    .CLK(_74typeflipflop_16_loaded_a[4]), .Data(_74typeflipflop_8_loaded_a[2]), .Load_A(and_111_out[4]),
    .Load_B(and_87_out[4]), .Always(_74typeflipflop_63_always), .Loaded_A(driver_33_out[2]),
    .Loaded_B(driver_48_out[2]), .Reset(reset_10_out));
  _74TypeFlipFlop _74typeflipflop_64 (
    .CLK(_74typeflipflop_16_loaded_a[4]), .Data(_74typeflipflop_8_loaded_a[1]), .Load_A(and_111_out[4]),
    .Load_B(and_87_out[4]), .Always(_74typeflipflop_64_always), .Loaded_A(driver_33_out[1]),
    .Loaded_B(driver_48_out[1]), .Reset(reset_10_out));
  _74TypeFlipFlop _74typeflipflop_65 (
    .CLK(_74typeflipflop_16_loaded_a[4]), .Data(_74typeflipflop_8_loaded_a[0]), .Load_A(and_111_out[4]),
    .Load_B(and_87_out[4]), .Always(_74typeflipflop_65_always), .Loaded_A(driver_33_out[0]),
    .Loaded_B(driver_48_out[0]), .Reset(reset_10_out));
  _74TypeFlipFlop _74typeflipflop_66 (
    .CLK(_74typeflipflop_16_loaded_a[5]), .Data(_74typeflipflop_8_loaded_a[7]), .Load_A(and_111_out[5]),
    .Load_B(and_87_out[5]), .Always(_74typeflipflop_66_always), .Loaded_A(driver_33_out[7]),
    .Loaded_B(driver_48_out[7]), .Reset(reset_11_out));
  _74TypeFlipFlop _74typeflipflop_67 (
    .CLK(_74typeflipflop_16_loaded_a[5]), .Data(_74typeflipflop_8_loaded_a[6]), .Load_A(and_111_out[5]),
    .Load_B(and_87_out[5]), .Always(_74typeflipflop_67_always), .Loaded_A(driver_33_out[6]),
    .Loaded_B(driver_48_out[6]), .Reset(reset_11_out));
  _74TypeFlipFlop _74typeflipflop_68 (
    .CLK(_74typeflipflop_16_loaded_a[5]), .Data(_74typeflipflop_8_loaded_a[5]), .Load_A(and_111_out[5]),
    .Load_B(and_87_out[5]), .Always(_74typeflipflop_68_always), .Loaded_A(driver_33_out[5]),
    .Loaded_B(driver_48_out[5]), .Reset(reset_11_out));
  _74TypeFlipFlop _74typeflipflop_69 (
    .CLK(_74typeflipflop_16_loaded_a[5]), .Data(_74typeflipflop_8_loaded_a[4]), .Load_A(and_111_out[5]),
    .Load_B(and_87_out[5]), .Always(_74typeflipflop_69_always), .Loaded_A(driver_33_out[4]),
    .Loaded_B(driver_48_out[4]), .Reset(reset_11_out));
  _74TypeFlipFlop _74typeflipflop_70 (
    .CLK(_74typeflipflop_16_loaded_a[5]), .Data(_74typeflipflop_8_loaded_a[3]), .Load_A(and_111_out[5]),
    .Load_B(and_87_out[5]), .Always(_74typeflipflop_70_always), .Loaded_A(driver_33_out[3]),
    .Loaded_B(driver_48_out[3]), .Reset(reset_11_out));
  _74TypeFlipFlop _74typeflipflop_71 (
    .CLK(_74typeflipflop_16_loaded_a[5]), .Data(_74typeflipflop_8_loaded_a[2]), .Load_A(and_111_out[5]),
    .Load_B(and_87_out[5]), .Always(_74typeflipflop_71_always), .Loaded_A(driver_33_out[2]),
    .Loaded_B(driver_48_out[2]), .Reset(reset_11_out));
  _74TypeFlipFlop _74typeflipflop_72 (
    .CLK(_74typeflipflop_16_loaded_a[5]), .Data(_74typeflipflop_8_loaded_a[1]), .Load_A(and_111_out[5]),
    .Load_B(and_87_out[5]), .Always(_74typeflipflop_72_always), .Loaded_A(driver_33_out[1]),
    .Loaded_B(driver_48_out[1]), .Reset(reset_11_out));
  _74TypeFlipFlop _74typeflipflop_73 (
    .CLK(_74typeflipflop_16_loaded_a[5]), .Data(_74typeflipflop_8_loaded_a[0]), .Load_A(and_111_out[5]),
    .Load_B(and_87_out[5]), .Always(_74typeflipflop_73_always), .Loaded_A(driver_33_out[0]),
    .Loaded_B(driver_48_out[0]), .Reset(reset_11_out));
  assign driver_48_out[0] = OPCODE[6] ? ARG2[0] : 1'bz;  // Driver driver_49
  assign driver_48_out[1] = OPCODE[6] ? ARG2[1] : 1'bz;  // Driver driver_50
  assign driver_33_out[0] = OPCODE[7] ? ARG1[0] : 1'bz;  // Driver driver_51
  assign driver_33_out[1] = OPCODE[7] ? ARG1[1] : 1'bz;  // Driver driver_52
  assign driver_48_out[0] = and_67_out ? rom_1_d[0] : 1'bz;  // Driver driver_53
  assign driver_33_out[0] = and_93_out ? rom_1_d[0] : 1'bz;  // Driver driver_54
  assign driver_48_out[2] = OPCODE[6] ? ARG2[2] : 1'bz;  // Driver driver_55
  assign driver_48_out[3] = OPCODE[6] ? ARG2[3] : 1'bz;  // Driver driver_56
  assign driver_33_out[2] = OPCODE[7] ? ARG1[2] : 1'bz;  // Driver driver_57
  assign driver_33_out[3] = OPCODE[7] ? ARG1[3] : 1'bz;  // Driver driver_58
  assign driver_48_out[1] = and_67_out ? rom_1_d[1] : 1'bz;  // Driver driver_59
  assign driver_48_out[2] = and_67_out ? rom_1_d[2] : 1'bz;  // Driver driver_60
  assign driver_33_out[1] = and_93_out ? rom_1_d[1] : 1'bz;  // Driver driver_61
  assign driver_33_out[2] = and_93_out ? rom_1_d[2] : 1'bz;  // Driver driver_62
  assign driver_48_out[4] = OPCODE[6] ? ARG2[4] : 1'bz;  // Driver driver_63
  assign driver_48_out[5] = OPCODE[6] ? ARG2[5] : 1'bz;  // Driver driver_64
  assign driver_33_out[4] = OPCODE[7] ? ARG1[4] : 1'bz;  // Driver driver_65
  assign driver_33_out[5] = OPCODE[7] ? ARG1[5] : 1'bz;  // Driver driver_66
  assign driver_48_out[3] = and_67_out ? rom_1_d[3] : 1'bz;  // Driver driver_67
  assign driver_48_out[4] = and_67_out ? rom_1_d[4] : 1'bz;  // Driver driver_68
  assign driver_33_out[3] = and_93_out ? rom_1_d[3] : 1'bz;  // Driver driver_69
  assign driver_33_out[4] = and_93_out ? rom_1_d[4] : 1'bz;  // Driver driver_70
  assign driver_48_out[6] = OPCODE[6] ? ARG2[6] : 1'bz;  // Driver driver_71
  assign driver_48_out[7] = OPCODE[6] ? ARG2[7] : 1'bz;  // Driver driver_72
  assign driver_33_out[6] = OPCODE[7] ? ARG1[6] : 1'bz;  // Driver driver_73
  assign driver_33_out[7] = OPCODE[7] ? ARG1[7] : 1'bz;  // Driver driver_74
  assign driver_48_out[5] = and_67_out ? rom_1_d[5] : 1'bz;  // Driver driver_75
  assign driver_48_out[6] = and_67_out ? rom_1_d[6] : 1'bz;  // Driver driver_76
  assign driver_33_out[5] = and_93_out ? rom_1_d[5] : 1'bz;  // Driver driver_77
  assign driver_33_out[6] = and_93_out ? rom_1_d[6] : 1'bz;  // Driver driver_78
  assign driver_48_out[7] = and_67_out ? rom_1_d[7] : 1'bz;  // Driver driver_79
  assign driver_33_out[7] = and_93_out ? rom_1_d[7] : 1'bz;  // Driver driver_80
  LED led_449 (.in(_74typeflipflop_41_always[7]));
  LED led_450 (.in(_74typeflipflop_41_always[6]));
  LED led_451 (.in(_74typeflipflop_41_always[5]));
  LED led_452 (.in(_74typeflipflop_41_always[4]));
  LED led_453 (.in(_74typeflipflop_41_always[3]));
  LED led_454 (.in(_74typeflipflop_41_always[2]));
  LED led_455 (.in(_74typeflipflop_41_always[1]));
  LED led_456 (.in(_74typeflipflop_41_always[0]));
  // NotConnected on nothing
  xor xor_17 (xor_17_out, driver_48_out[7], 1'b1);
  xor xor_18 (xor_18_out, driver_48_out[6], 1'b1);
  xor xor_19 (xor_19_out, driver_48_out[5], 1'b1);
  xor xor_20 (xor_20_out, 1'b1, driver_48_out[4]);
  xor xor_21 (xor_21_out, 1'b1, driver_48_out[3]);
  xor xor_22 (xor_22_out, 1'b1, driver_48_out[2]);
  xor xor_23 (xor_23_out, 1'b1, driver_48_out[1]);
  xor xor_24 (xor_24_out, 1'b1, driver_48_out[0]);
  and and_112 (and_112_out, xor_17_out, driver_33_out[7]);
  xor xor_25 (xor_25_out, xor_17_out, driver_33_out[7]);
  and and_113 (and_113_out, xor_18_out, driver_33_out[6]);
  xor xor_26 (xor_26_out, xor_18_out, driver_33_out[6]);
  and and_114 (and_114_out, xor_19_out, driver_33_out[5]);
  xor xor_27 (xor_27_out, xor_19_out, driver_33_out[5]);
  and and_115 (and_115_out, xor_20_out, driver_33_out[4]);
  xor xor_28 (xor_28_out, xor_20_out, driver_33_out[4]);
  and and_116 (and_116_out, xor_21_out, driver_33_out[3]);
  xor xor_29 (xor_29_out, xor_21_out, driver_33_out[3]);
  and and_117 (and_117_out, xor_22_out, driver_33_out[2]);
  xor xor_30 (xor_30_out, xor_22_out, driver_33_out[2]);
  and and_118 (and_118_out, xor_23_out, driver_33_out[1]);
  xor xor_31 (xor_31_out, xor_23_out, driver_33_out[1]);
  and and_119 (and_119_out, xor_24_out, driver_33_out[0]);
  xor xor_32 (xor_32_out, xor_24_out, driver_33_out[0]);
  xor xor_33 (xor_33_out, driver_48_out[7], and_241_out);
  xor xor_34 (xor_34_out, driver_48_out[6], and_241_out);
  xor xor_35 (xor_35_out, driver_48_out[5], and_241_out);
  xor xor_36 (xor_36_out, and_241_out, driver_48_out[4]);
  xor xor_37 (xor_37_out, and_241_out, driver_48_out[3]);
  xor xor_38 (xor_38_out, and_241_out, driver_48_out[2]);
  xor xor_39 (xor_39_out, and_241_out, driver_48_out[1]);
  xor xor_40 (xor_40_out, and_241_out, driver_48_out[0]);
  and and_120 (and_175_out[0], driver_48_out[0], driver_33_out[0]);
  nand nand_1 (nand_8_out[0], driver_48_out[0], driver_33_out[0]);
  or or_16 (or_25_out[0], driver_48_out[0], driver_33_out[0]);
  nor nor_1 (nor_8_out[0], driver_48_out[0], driver_33_out[0]);
  xor xor_41 (xor_56_out[0], driver_48_out[0], driver_33_out[0]);
  and and_121 (and_121_out, xor_33_out, driver_33_out[7]);
  xor xor_42 (xor_42_out, xor_33_out, driver_33_out[7]);
  and and_122 (and_122_out, xor_34_out, driver_33_out[6]);
  xor xor_43 (xor_43_out, xor_34_out, driver_33_out[6]);
  and and_123 (and_123_out, xor_35_out, driver_33_out[5]);
  xor xor_44 (xor_44_out, xor_35_out, driver_33_out[5]);
  and and_124 (and_124_out, xor_36_out, driver_33_out[4]);
  xor xor_45 (xor_45_out, xor_36_out, driver_33_out[4]);
  and and_125 (and_125_out, xor_37_out, driver_33_out[3]);
  xor xor_46 (xor_46_out, xor_37_out, driver_33_out[3]);
  and and_126 (and_126_out, xor_38_out, driver_33_out[2]);
  xor xor_47 (xor_47_out, xor_38_out, driver_33_out[2]);
  and and_127 (and_127_out, xor_39_out, driver_33_out[1]);
  xor xor_48 (xor_48_out, xor_39_out, driver_33_out[1]);
  and and_128 (and_128_out, xor_40_out, driver_33_out[0]);
  xor xor_49 (xor_49_out, xor_40_out, driver_33_out[0]);
  and and_129 (and_175_out[1], driver_48_out[1], driver_33_out[1]);
  nand nand_2 (nand_8_out[1], driver_48_out[1], driver_33_out[1]);
  or or_17 (or_25_out[1], driver_48_out[1], driver_33_out[1]);
  nor nor_2 (nor_8_out[1], driver_48_out[1], driver_33_out[1]);
  xor xor_50 (xor_56_out[1], driver_48_out[1], driver_33_out[1]);
  and and_130 (and_130_out, or_40_out, xor_28_out);
  and and_131 (and_131_out, xor_27_out, xor_26_out);
  and and_132 (and_132_out, and_115_out, xor_27_out);
  and and_133 (and_133_out, xor_26_out, xor_25_out);
  and and_134 (and_134_out, xor_25_out, xor_26_out);
  and and_135 (and_135_out, and_113_out, xor_25_out);
  and and_136 (and_136_out, xor_26_out, xor_27_out);
  and and_137 (and_137_out, xor_28_out, or_40_out);
  and and_138 (and_138_out, xor_27_out, xor_26_out);
  and and_139 (and_139_out, and_114_out, xor_26_out);
  and and_140 (and_140_out, xor_28_out, xor_27_out);
  and and_141 (and_141_out, xor_27_out, and_115_out);
  and and_142 (and_142_out, xor_28_out, or_40_out);
  and and_143 (and_143_out, 1'b1, xor_32_out);
  and and_144 (and_144_out, xor_31_out, xor_30_out);
  and and_145 (and_145_out, and_119_out, xor_31_out);
  and and_146 (and_146_out, xor_30_out, xor_29_out);
  and and_147 (and_147_out, xor_29_out, xor_30_out);
  and and_148 (and_148_out, and_117_out, xor_29_out);
  and and_149 (and_149_out, xor_30_out, xor_31_out);
  and and_150 (and_150_out, xor_32_out, 1'b1);
  and and_151 (and_151_out, xor_31_out, xor_30_out);
  and and_152 (and_152_out, and_118_out, xor_30_out);
  and and_153 (and_153_out, xor_32_out, xor_31_out);
  and and_154 (and_154_out, xor_31_out, and_119_out);
  and and_155 (and_155_out, xor_32_out, 1'b1);
  and and_156 (and_175_out[2], driver_48_out[2], driver_33_out[2]);
  and and_157 (and_175_out[3], driver_48_out[3], driver_33_out[3]);
  nand nand_3 (nand_8_out[2], driver_48_out[2], driver_33_out[2]);
  nand nand_4 (nand_8_out[3], driver_48_out[3], driver_33_out[3]);
  or or_18 (or_25_out[2], driver_48_out[2], driver_33_out[2]);
  or or_19 (or_25_out[3], driver_48_out[3], driver_33_out[3]);
  nor nor_3 (nor_8_out[2], driver_48_out[2], driver_33_out[2]);
  nor nor_4 (nor_8_out[3], driver_48_out[3], driver_33_out[3]);
  xor xor_51 (xor_56_out[2], driver_48_out[2], driver_33_out[2]);
  xor xor_52 (xor_56_out[3], driver_48_out[3], driver_33_out[3]);
  and and_158 (and_175_out[4], driver_48_out[4], driver_33_out[4]);
  nand nand_5 (nand_8_out[4], driver_48_out[4], driver_33_out[4]);
  or or_20 (or_25_out[4], driver_48_out[4], driver_33_out[4]);
  nor nor_5 (nor_8_out[4], driver_48_out[4], driver_33_out[4]);
  xor xor_53 (xor_56_out[4], driver_48_out[4], driver_33_out[4]);
  and and_159 (and_159_out, and_130_out, and_131_out);
  and and_160 (and_160_out, and_132_out, and_133_out);
  and and_161 (and_161_out, and_134_out, and_114_out);
  and and_162 (and_162_out, and_136_out, and_137_out);
  and and_163 (and_163_out, and_138_out, and_115_out);
  and and_164 (and_164_out, and_140_out, or_40_out);
  or or_21 (or_21_out, and_142_out, and_115_out);
  and and_165 (and_165_out, and_143_out, and_144_out);
  and and_166 (and_166_out, and_145_out, and_146_out);
  and and_167 (and_167_out, and_147_out, and_118_out);
  and and_168 (and_168_out, and_149_out, and_150_out);
  and and_169 (and_169_out, and_151_out, and_119_out);
  and and_170 (and_170_out, and_153_out, 1'b1);
  or or_22 (or_22_out, and_155_out, and_119_out);
  and and_171 (and_175_out[5], driver_48_out[5], driver_33_out[5]);
  nand nand_6 (nand_8_out[5], driver_48_out[5], driver_33_out[5]);
  or or_23 (or_25_out[5], driver_48_out[5], driver_33_out[5]);
  nor nor_6 (nor_8_out[5], driver_48_out[5], driver_33_out[5]);
  xor xor_54 (xor_56_out[5], driver_48_out[5], driver_33_out[5]);
  and and_172 (and_172_out, and_159_out, xor_25_out);
  and and_173 (and_173_out, and_165_out, xor_29_out);
  and and_174 (and_175_out[6], driver_48_out[6], driver_33_out[6]);
  and and_175 (and_175_out[7], driver_48_out[7], driver_33_out[7]);
  nand nand_7 (nand_8_out[6], driver_48_out[6], driver_33_out[6]);
  nand nand_8 (nand_8_out[7], driver_48_out[7], driver_33_out[7]);
  or or_24 (or_25_out[6], driver_48_out[6], driver_33_out[6]);
  or or_25 (or_25_out[7], driver_48_out[7], driver_33_out[7]);
  nor nor_7 (nor_8_out[6], driver_48_out[6], driver_33_out[6]);
  nor nor_8 (nor_8_out[7], driver_48_out[7], driver_33_out[7]);
  xor xor_55 (xor_56_out[6], driver_48_out[6], driver_33_out[6]);
  xor xor_56 (xor_56_out[7], driver_48_out[7], driver_33_out[7]);
  or or_26 (or_26_out, and_162_out, and_163_out);
  or or_27 (or_27_out, and_139_out, and_113_out);
  or or_28 (or_28_out, and_164_out, and_141_out);
  or or_29 (or_29_out, and_168_out, and_169_out);
  or or_30 (or_30_out, and_152_out, and_117_out);
  or or_31 (or_31_out, and_170_out, and_154_out);
  or or_32 (or_32_out, or_28_out, and_114_out);
  or or_33 (or_33_out, or_31_out, and_118_out);
  assign driver_116_out[0] = and_242_out ? and_175_out[0] : 1'bz;  // Driver driver_81
  assign driver_116_out[0] = and_243_out ? nand_8_out[0] : 1'bz;  // Driver driver_82
  assign driver_116_out[0] = and_244_out ? or_25_out[0] : 1'bz;  // Driver driver_83
  assign driver_116_out[0] = and_245_out ? nor_8_out[0] : 1'bz;  // Driver driver_84
  assign driver_116_out[0] = and_246_out ? xor_56_out[0] : 1'bz;  // Driver driver_85
  or or_34 (or_34_out, and_161_out, and_135_out);
  or or_35 (or_35_out, or_42_out, or_34_out);
  or or_36 (or_36_out, or_35_out, and_112_out);
  or or_37 (or_37_out, or_26_out, or_27_out);
  or or_38 (or_38_out, and_167_out, and_148_out);
  or or_39 (or_39_out, or_43_out, or_38_out);
  or or_40 (or_40_out, or_39_out, and_116_out);
  or or_41 (or_41_out, or_29_out, or_30_out);
  assign driver_116_out[1] = and_242_out ? and_175_out[1] : 1'bz;  // Driver driver_86
  assign driver_116_out[2] = and_242_out ? and_175_out[2] : 1'bz;  // Driver driver_87
  assign driver_116_out[1] = and_243_out ? nand_8_out[1] : 1'bz;  // Driver driver_88
  assign driver_116_out[2] = and_243_out ? nand_8_out[2] : 1'bz;  // Driver driver_89
  assign driver_116_out[1] = and_244_out ? or_25_out[1] : 1'bz;  // Driver driver_90
  assign driver_116_out[2] = and_244_out ? or_25_out[2] : 1'bz;  // Driver driver_91
  assign driver_116_out[1] = and_245_out ? nor_8_out[1] : 1'bz;  // Driver driver_92
  assign driver_116_out[2] = and_245_out ? nor_8_out[2] : 1'bz;  // Driver driver_93
  assign driver_116_out[1] = and_246_out ? xor_56_out[1] : 1'bz;  // Driver driver_94
  assign driver_116_out[2] = and_246_out ? xor_56_out[2] : 1'bz;  // Driver driver_95
  or or_42 (or_42_out, and_172_out, and_160_out);
  xor xor_57 (xor_57_out[7], xor_25_out, or_37_out);
  xor xor_58 (xor_57_out[6], xor_26_out, or_32_out);
  xor xor_59 (xor_57_out[5], xor_27_out, or_21_out);
  xor xor_60 (xor_57_out[4], or_40_out, xor_28_out);
  or or_43 (or_43_out, and_173_out, and_166_out);
  xor xor_61 (xor_57_out[3], xor_29_out, or_41_out);
  xor xor_62 (xor_57_out[2], xor_30_out, or_33_out);
  xor xor_63 (xor_57_out[1], xor_31_out, or_22_out);
  xor xor_64 (xor_57_out[0], 1'b1, xor_32_out);
  assign driver_116_out[3] = and_242_out ? and_175_out[3] : 1'bz;  // Driver driver_96
  assign driver_116_out[4] = and_242_out ? and_175_out[4] : 1'bz;  // Driver driver_97
  assign driver_116_out[3] = and_243_out ? nand_8_out[3] : 1'bz;  // Driver driver_98
  assign driver_116_out[4] = and_243_out ? nand_8_out[4] : 1'bz;  // Driver driver_99
  assign driver_116_out[3] = and_244_out ? or_25_out[3] : 1'bz;  // Driver driver_100
  assign driver_116_out[4] = and_244_out ? or_25_out[4] : 1'bz;  // Driver driver_101
  assign driver_116_out[3] = and_245_out ? nor_8_out[3] : 1'bz;  // Driver driver_102
  assign driver_116_out[4] = and_245_out ? nor_8_out[4] : 1'bz;  // Driver driver_103
  assign driver_116_out[3] = and_246_out ? xor_56_out[3] : 1'bz;  // Driver driver_104
  assign driver_116_out[4] = and_246_out ? xor_56_out[4] : 1'bz;  // Driver driver_105
  and and_176 (and_176_out, or_57_out, xor_45_out);
  and and_177 (and_177_out, xor_44_out, xor_43_out);
  and and_178 (and_178_out, and_124_out, xor_44_out);
  and and_179 (and_179_out, xor_43_out, xor_42_out);
  and and_180 (and_180_out, xor_42_out, xor_43_out);
  and and_181 (and_181_out, and_122_out, xor_42_out);
  and and_182 (and_182_out, xor_43_out, xor_44_out);
  and and_183 (and_183_out, xor_45_out, or_57_out);
  and and_184 (and_184_out, xor_44_out, xor_43_out);
  and and_185 (and_185_out, and_123_out, xor_43_out);
  and and_186 (and_186_out, xor_45_out, xor_44_out);
  and and_187 (and_187_out, xor_44_out, and_124_out);
  and and_188 (and_188_out, xor_45_out, or_57_out);
  and and_189 (and_189_out, and_241_out, xor_49_out);
  and and_190 (and_190_out, xor_48_out, xor_47_out);
  and and_191 (and_191_out, and_128_out, xor_48_out);
  and and_192 (and_192_out, xor_47_out, xor_46_out);
  and and_193 (and_193_out, xor_46_out, xor_47_out);
  and and_194 (and_194_out, and_126_out, xor_46_out);
  and and_195 (and_195_out, xor_47_out, xor_48_out);
  and and_196 (and_196_out, xor_49_out, and_241_out);
  and and_197 (and_197_out, xor_48_out, xor_47_out);
  and and_198 (and_198_out, and_127_out, xor_47_out);
  and and_199 (and_199_out, xor_49_out, xor_48_out);
  and and_200 (and_200_out, xor_48_out, and_128_out);
  and and_201 (and_201_out, xor_49_out, and_241_out);
  assign driver_116_out[5] = and_242_out ? and_175_out[5] : 1'bz;  // Driver driver_106
  assign driver_116_out[6] = and_242_out ? and_175_out[6] : 1'bz;  // Driver driver_107
  assign driver_116_out[5] = and_243_out ? nand_8_out[5] : 1'bz;  // Driver driver_108
  assign driver_116_out[6] = and_243_out ? nand_8_out[6] : 1'bz;  // Driver driver_109
  assign driver_116_out[5] = and_244_out ? or_25_out[5] : 1'bz;  // Driver driver_110
  assign driver_116_out[6] = and_244_out ? or_25_out[6] : 1'bz;  // Driver driver_111
  assign driver_116_out[5] = and_245_out ? nor_8_out[5] : 1'bz;  // Driver driver_112
  assign driver_116_out[6] = and_245_out ? nor_8_out[6] : 1'bz;  // Driver driver_113
  assign driver_116_out[5] = and_246_out ? xor_56_out[5] : 1'bz;  // Driver driver_114
  assign driver_116_out[6] = and_246_out ? xor_56_out[6] : 1'bz;  // Driver driver_115
  and and_202 (and_202_out, and_176_out, and_177_out);
  and and_203 (and_203_out, and_178_out, and_179_out);
  and and_204 (and_204_out, and_180_out, and_123_out);
  and and_205 (and_205_out, and_182_out, and_183_out);
  and and_206 (and_206_out, and_184_out, and_124_out);
  and and_207 (and_207_out, and_186_out, or_57_out);
  and and_208 (and_208_out, and_189_out, and_190_out);
  and and_209 (and_209_out, and_191_out, and_192_out);
  and and_210 (and_210_out, and_193_out, and_127_out);
  and and_211 (and_211_out, and_195_out, and_196_out);
  and and_212 (and_212_out, and_197_out, and_128_out);
  and and_213 (and_213_out, and_199_out, and_241_out);
  assign driver_116_out[7] = and_242_out ? and_175_out[7] : 1'bz;  // Driver driver_116
  assign driver_116_out[7] = and_243_out ? nand_8_out[7] : 1'bz;  // Driver driver_117
  assign driver_116_out[7] = and_244_out ? or_25_out[7] : 1'bz;  // Driver driver_118
  assign driver_116_out[7] = and_245_out ? nor_8_out[7] : 1'bz;  // Driver driver_119
  assign driver_116_out[7] = and_246_out ? xor_56_out[7] : 1'bz;  // Driver driver_120
  or or_44 (or_44_out, and_188_out, and_124_out);
  or or_45 (or_45_out, and_201_out, and_128_out);
  and and_214 (and_214_out, and_202_out, xor_42_out);
  or or_46 (or_46_out, and_207_out, and_187_out);
  and and_215 (and_215_out, and_208_out, xor_46_out);
  or or_47 (or_47_out, and_213_out, and_200_out);
  or or_48 (or_48_out, and_205_out, and_206_out);
  or or_49 (or_49_out, and_185_out, and_122_out);
  or or_50 (or_50_out, and_211_out, and_212_out);
  or or_51 (or_51_out, and_198_out, and_126_out);
  or or_52 (or_52_out, and_204_out, and_181_out);
  or or_53 (or_53_out, or_61_out, and_121_out);
  or or_54 (or_54_out, or_48_out, or_49_out);
  or or_55 (or_55_out, or_46_out, and_123_out);
  or or_56 (or_56_out, and_210_out, and_194_out);
  or or_57 (or_57_out, or_63_out, and_125_out);
  or or_58 (or_58_out, or_50_out, or_51_out);
  or or_59 (or_59_out, or_47_out, and_127_out);
  or or_60 (or_60_out, and_214_out, and_203_out);
  or or_61 (or_61_out, or_60_out, or_52_out);
  or or_62 (or_62_out, and_215_out, and_209_out);
  or or_63 (or_63_out, or_62_out, or_56_out);
  xor xor_65 (xor_69_out[7], xor_42_out, or_54_out);
  xor xor_66 (xor_69_out[6], xor_43_out, or_55_out);
  xor xor_67 (xor_69_out[5], xor_44_out, or_44_out);
  xor xor_68 (xor_69_out[4], or_57_out, xor_45_out);
  xor xor_69 (xor_69_out[3], xor_46_out, or_58_out);
  xor xor_70 (xor_69_out[2], xor_47_out, or_59_out);
  xor xor_71 (xor_69_out[1], xor_48_out, or_45_out);
  xor xor_72 (xor_69_out[0], and_241_out, xor_49_out);
  not not_36 (not_36_out, OPCODE[2]);
  not not_37 (not_37_out, OPCODE[1]);
  not not_38 (not_38_out, OPCODE[0]);
  not not_39 (not_39_out, OPCODE[1]);
  not not_40 (not_40_out, OPCODE[0]);
  and and_216 (and_216_out, not_38_out, not_37_out);
  and and_217 (and_217_out, OPCODE[0], not_37_out);
  and and_218 (and_218_out, not_38_out, OPCODE[1]);
  and and_219 (and_219_out, OPCODE[1], OPCODE[0]);
  not not_41 (not_41_out, OPCODE[2]);
  and and_220 (and_220_out, not_40_out, not_39_out);
  and and_221 (and_221_out, OPCODE[0], not_39_out);
  and and_222 (and_222_out, not_40_out, OPCODE[1]);
  and and_223 (and_223_out, OPCODE[1], OPCODE[0]);
  not not_42 (not_42_out, not_36_out);
  and and_224 (and_224_out, and_216_out, not_41_out);
  and and_225 (and_225_out, and_217_out, not_41_out);
  and and_226 (and_226_out, and_218_out, not_41_out);
  and and_227 (and_227_out, and_219_out, not_41_out);
  and and_228 (and_228_out, and_220_out, not_42_out);
  and and_229 (and_229_out, and_221_out, not_42_out);
  and and_230 (and_230_out, and_222_out, not_42_out);
  // And and_231 has open pins: In_1=and_223_out, In_2=not_42_out, out=open
  or or_64 (or_64_out, xor_57_out[7], xor_57_out[6]);
  or or_65 (or_65_out, xor_57_out[5], xor_57_out[4]);
  or or_66 (or_66_out, xor_57_out[3], xor_57_out[2]);
  or or_67 (or_67_out, xor_57_out[1], xor_57_out[0]);
  not not_43 (not_43_out, OPCODE[2]);
  assign driver_116_out[0] = or_79_out ? xor_69_out[0] : 1'bz;  // Driver driver_121
  or or_68 (or_68_out, or_64_out, or_65_out);
  or or_69 (or_69_out, or_66_out, or_67_out);
  not not_44 (not_44_out, OPCODE[1]);
  not not_45 (not_45_out, OPCODE[1]);
  assign driver_116_out[1] = or_79_out ? xor_69_out[1] : 1'bz;  // Driver driver_122
  assign driver_116_out[2] = or_79_out ? xor_69_out[2] : 1'bz;  // Driver driver_123
  or or_70 (or_70_out, or_68_out, or_69_out);
  not not_46 (not_46_out, OPCODE[0]);
  and and_232 (and_232_out, not_46_out, not_44_out);
  and and_233 (and_233_out, OPCODE[0], not_44_out);
  and and_234 (and_234_out, not_46_out, OPCODE[1]);
  and and_235 (and_235_out, OPCODE[1], OPCODE[0]);
  not not_47 (not_47_out, OPCODE[2]);
  not not_48 (not_48_out, OPCODE[0]);
  and and_236 (and_236_out, not_48_out, not_45_out);
  and and_237 (and_237_out, OPCODE[0], not_45_out);
  and and_238 (and_238_out, not_48_out, OPCODE[1]);
  and and_239 (and_239_out, OPCODE[1], OPCODE[0]);
  not not_49 (not_49_out, not_43_out);
  assign driver_116_out[3] = or_79_out ? xor_69_out[3] : 1'bz;  // Driver driver_124
  assign driver_116_out[4] = or_79_out ? xor_69_out[4] : 1'bz;  // Driver driver_125
  assign driver_116_out[5] = or_79_out ? xor_69_out[5] : 1'bz;  // Driver driver_126
  assign driver_116_out[6] = or_79_out ? xor_69_out[6] : 1'bz;  // Driver driver_127
  and and_240 (and_240_out, and_232_out, not_47_out);
  and and_241 (and_241_out, and_233_out, not_47_out);
  and and_242 (and_242_out, and_234_out, not_47_out);
  and and_243 (and_243_out, and_235_out, not_47_out);
  and and_244 (and_244_out, and_236_out, not_49_out);
  and and_245 (and_245_out, and_237_out, not_49_out);
  and and_246 (and_246_out, and_238_out, not_49_out);
  // And and_247 has open pins: In_1=and_239_out, In_2=not_49_out, out=open
  assign driver_116_out[7] = or_79_out ? xor_69_out[7] : 1'bz;  // Driver driver_128
  or or_71 (or_71_out, and_229_out, or_72_out);
  or or_72 (or_72_out, and_228_out, and_224_out);
  or or_73 (or_73_out, and_226_out, and_228_out);
  or or_74 (or_74_out, and_227_out, and_229_out);
  or or_75 (or_75_out, and_250_out, and_251_out);
  or or_76 (or_76_out, or_75_out, and_230_out);
  or or_77 (or_77_out, or_78_out, or_76_out);
  and and_248 (and_248_out, and_75_out, or_77_out);
  not not_50 (not_50_out, or_70_out);
  not not_51 (not_51_out, xor_57_out[7]);
  or or_78 (or_78_out, and_249_out, and_252_out);
  and and_249 (and_249_out, or_71_out, not_50_out);
  and and_250 (and_250_out, or_70_out, and_225_out);
  and and_251 (and_251_out, or_73_out, not_51_out);
  and and_252 (and_252_out, xor_57_out[7], or_74_out);
  or or_79 (or_79_out, and_240_out, and_241_out);
  assign pulldown_1_out[0] = and_74_out ? driver_116_out[0] : 1'bz;  // Driver driver_129
  assign pulldown_1_out[1] = and_74_out ? driver_116_out[1] : 1'bz;  // Driver driver_130
  assign pulldown_1_out[2] = and_74_out ? driver_116_out[2] : 1'bz;  // Driver driver_131
  assign pulldown_1_out[3] = and_74_out ? driver_116_out[3] : 1'bz;  // Driver driver_132
  assign pulldown_1_out[4] = and_74_out ? driver_116_out[4] : 1'bz;  // Driver driver_133
  assign pulldown_1_out[5] = and_74_out ? driver_116_out[5] : 1'bz;  // Driver driver_134
  assign pulldown_1_out[6] = and_74_out ? driver_116_out[6] : 1'bz;  // Driver driver_135
  assign pulldown_1_out[7] = and_74_out ? driver_116_out[7] : 1'bz;  // Driver driver_136
  // NotConnected on notconnected_7_out
  // NotConnected on notconnected_8_out
  // NotConnected on notconnected_9_out
  // NotConnected on notconnected_10_out
  DipSwitch dipswitch_5 (.out(dipswitch_5_out));
  DipSwitch dipswitch_6 (.out(dipswitch_6_out));
  DipSwitch dipswitch_7 (.out(dipswitch_7_out));
  // NotConnected on notconnected_11_out
  nand nand_9 (nand_9_out, nand_12_out, nand_10_out);
  nand nand_10 (nand_10_out, nand_9_out, dipswitch_5_out);
  nand nand_11 (nand_11_out, nand_10_out, dipswitch_5_out, nand_12_out);
  nand nand_12 (nand_12_out, nand_11_out, NormalRegTest[6]);
  nand nand_13 (nand_13_out, nand_16_out, nand_14_out);
  nand nand_14 (nand_14_out, nand_13_out, dipswitch_5_out);
  nand nand_15 (nand_15_out, nand_14_out, dipswitch_5_out, nand_16_out);
  nand nand_16 (nand_16_out, nand_15_out, NormalRegTest[4]);
  nand nand_17 (nand_17_out, nand_20_out, nand_18_out);
  nand nand_18 (nand_18_out, nand_17_out, dipswitch_5_out);
  nand nand_19 (nand_19_out, nand_18_out, dipswitch_5_out, nand_20_out);
  nand nand_20 (nand_20_out, nand_19_out, NormalRegTest[2]);
  nand nand_21 (nand_21_out, nand_24_out, nand_22_out);
  nand nand_22 (nand_22_out, nand_21_out, dipswitch_5_out);
  nand nand_23 (nand_23_out, nand_22_out, dipswitch_5_out, nand_24_out);
  nand nand_24 (nand_24_out, nand_23_out, NormalRegTest[0]);
  DipSwitch dipswitch_8 (.out(dipswitch_8_out));
  DipSwitch dipswitch_9 (.out(dipswitch_9_out));
  DipSwitch dipswitch_10 (.out(dipswitch_10_out));
  not not_52 (not_52_out, notconnected_9_out[7]);
  and and_253 (and_253_out, notconnected_7_out, notconnected_9_out[7]);
  not not_53 (not_53_out, notconnected_9_out[6]);
  and and_254 (and_254_out, notconnected_7_out, notconnected_9_out[6]);
  not not_54 (not_54_out, notconnected_9_out[5]);
  and and_255 (and_255_out, notconnected_7_out, notconnected_9_out[5]);
  not not_55 (not_55_out, notconnected_9_out[4]);
  and and_256 (and_256_out, notconnected_7_out, notconnected_9_out[4]);
  not not_56 (not_56_out, notconnected_9_out[3]);
  and and_257 (and_257_out, notconnected_7_out, notconnected_9_out[3]);
  not not_57 (not_57_out, notconnected_9_out[2]);
  and and_258 (and_258_out, notconnected_7_out, notconnected_9_out[2]);
  not not_58 (not_58_out, notconnected_9_out[1]);
  and and_259 (and_259_out, notconnected_7_out, notconnected_9_out[1]);
  not not_59 (not_59_out, notconnected_9_out[0]);
  and and_260 (and_260_out, notconnected_7_out, notconnected_9_out[0]);
  and and_261 (and_261_out, not_60_out, dipswitch_9_out);
  not not_60 (not_60_out, dipswitch_10_out);
  and and_262 (and_262_out, dipswitch_9_out, dipswitch_10_out);
  and and_263 (and_263_out, not_52_out, notconnected_7_out);
  and and_264 (and_264_out, not_53_out, notconnected_7_out);
  and and_265 (and_265_out, not_54_out, notconnected_7_out);
  and and_266 (and_266_out, not_55_out, notconnected_7_out);
  and and_267 (and_267_out, not_56_out, notconnected_7_out);
  and and_268 (and_268_out, not_57_out, notconnected_7_out);
  and and_269 (and_269_out, not_58_out, notconnected_7_out);
  and and_270 (and_270_out, not_59_out, notconnected_7_out);
  nand nand_25 (nand_25_out, nand_10_out, nand_26_out);
  nand nand_26 (nand_26_out, nand_25_out, nand_11_out);
  nand nand_27 (nand_27_out, nand_14_out, nand_28_out);
  nand nand_28 (nand_28_out, nand_27_out, nand_15_out);
  nand nand_29 (nand_29_out, nand_18_out, nand_30_out);
  nand nand_30 (nand_30_out, nand_29_out, nand_19_out);
  nand nand_31 (nand_31_out, nand_22_out, nand_32_out);
  nand nand_32 (nand_32_out, nand_31_out, nand_23_out);
  nor nor_9 (nor_9_out, and_263_out, nor_10_out);
  nor nor_10 (nor_10_out, nor_9_out, and_253_out);
  nor nor_11 (nor_11_out, and_264_out, nor_12_out);
  nor nor_12 (nor_12_out, nor_11_out, and_254_out);
  nor nor_13 (nor_13_out, and_265_out, nor_14_out);
  nor nor_14 (nor_14_out, nor_13_out, and_255_out);
  nor nor_15 (nor_15_out, and_266_out, nor_16_out);
  nor nor_16 (nor_16_out, nor_15_out, and_256_out);
  nor nor_17 (nor_17_out, and_267_out, nor_18_out);
  nor nor_18 (nor_18_out, nor_17_out, and_257_out);
  nor nor_19 (nor_19_out, and_268_out, nor_20_out);
  nor nor_20 (nor_20_out, nor_19_out, and_258_out);
  nor nor_21 (nor_21_out, and_269_out, nor_22_out);
  nor nor_22 (nor_22_out, nor_21_out, and_259_out);
  nor nor_23 (nor_23_out, and_270_out, nor_24_out);
  nor nor_24 (nor_24_out, nor_23_out, and_260_out);
  assign driver_137_out = dipswitch_6_out ? nand_25_out : 1'bz;  // Driver driver_137
  assign driver_138_out = dipswitch_7_out ? nand_25_out : 1'bz;  // Driver driver_138
  assign driver_139_out = dipswitch_6_out ? nand_27_out : 1'bz;  // Driver driver_139
  assign driver_140_out = dipswitch_7_out ? nand_27_out : 1'bz;  // Driver driver_140
  assign driver_141_out = dipswitch_6_out ? nand_29_out : 1'bz;  // Driver driver_141
  assign driver_142_out = dipswitch_7_out ? nand_29_out : 1'bz;  // Driver driver_142
  assign driver_143_out = dipswitch_6_out ? nand_31_out : 1'bz;  // Driver driver_143
  assign driver_144_out = dipswitch_7_out ? nand_31_out : 1'bz;  // Driver driver_144
  and and_271 (and_271_out, notconnected_10_out[7], notconnected_11_out[7]);
  xor xor_73 (xor_73_out, notconnected_11_out[7], notconnected_10_out[7]);
  and and_272 (and_272_out, notconnected_10_out[6], notconnected_11_out[6]);
  xor xor_74 (xor_74_out, notconnected_11_out[6], notconnected_10_out[6]);
  and and_273 (and_273_out, notconnected_10_out[5], notconnected_11_out[5]);
  xor xor_75 (xor_75_out, notconnected_11_out[5], notconnected_10_out[5]);
  and and_274 (and_274_out, notconnected_10_out[4], notconnected_11_out[4]);
  xor xor_76 (xor_76_out, notconnected_11_out[4], notconnected_10_out[4]);
  and and_275 (and_275_out, notconnected_10_out[3], notconnected_11_out[3]);
  xor xor_77 (xor_77_out, notconnected_11_out[3], notconnected_10_out[3]);
  and and_276 (and_276_out, notconnected_10_out[2], notconnected_11_out[2]);
  xor xor_78 (xor_78_out, notconnected_11_out[2], notconnected_10_out[2]);
  and and_277 (and_277_out, notconnected_10_out[1], notconnected_11_out[1]);
  xor xor_79 (xor_79_out, notconnected_11_out[1], notconnected_10_out[1]);
  and and_278 (and_278_out, notconnected_10_out[0], notconnected_11_out[0]);
  xor xor_80 (xor_80_out, notconnected_11_out[0], notconnected_10_out[0]);
  nor nor_25 (nor_25_out, and_261_out, nor_26_out);
  nor nor_26 (nor_26_out, nor_25_out, and_262_out);
  or or_80 (or_80_out, and_271_out, and_279_out);
  and and_279 (and_279_out, xor_73_out, or_81_out);
  xor xor_81 (xor_81_out, xor_73_out, or_81_out);
  or or_81 (or_81_out, and_272_out, and_280_out);
  and and_280 (and_280_out, xor_74_out, or_82_out);
  xor xor_82 (xor_82_out, xor_74_out, or_82_out);
  or or_82 (or_82_out, and_273_out, and_281_out);
  and and_281 (and_281_out, xor_75_out, or_83_out);
  xor xor_83 (xor_83_out, xor_75_out, or_83_out);
  or or_83 (or_83_out, and_274_out, and_282_out);
  and and_282 (and_282_out, xor_76_out, or_84_out);
  xor xor_84 (xor_84_out, xor_76_out, or_84_out);
  or or_84 (or_84_out, and_275_out, and_291_out);
  or or_85 (or_85_out, and_276_out, and_292_out);
  or or_86 (or_86_out, and_277_out, and_293_out);
  or or_87 (or_87_out, and_278_out, and_294_out);
  // NotConnected on notconnected_12_out
  Reset reset_12 ();  // open: out
  Reset reset_13 ();  // open: out
  and and_283 (and_283_out, nor_9_out, notconnected_8_out);
  Reset reset_14 ();  // open: out
  and and_284 (and_284_out, nor_11_out, notconnected_8_out);
  Reset reset_15 ();  // open: out
  and and_285 (and_285_out, nor_13_out, notconnected_8_out);
  Reset reset_16 ();  // open: out
  and and_286 (and_286_out, nor_15_out, notconnected_8_out);
  Reset reset_17 ();  // open: out
  and and_287 (and_287_out, nor_17_out, notconnected_8_out);
  Reset reset_18 ();  // open: out
  and and_288 (and_288_out, nor_19_out, notconnected_8_out);
  Reset reset_19 ();  // open: out
  and and_289 (and_289_out, nor_21_out, notconnected_8_out);
  Reset reset_20 ();  // open: out
  and and_290 (and_290_out, nor_23_out, notconnected_8_out);
  and and_291 (and_291_out, xor_77_out, or_85_out);
  xor xor_85 (xor_85_out, xor_77_out, or_85_out);
  and and_292 (and_292_out, xor_78_out, or_86_out);
  xor xor_86 (xor_86_out, xor_78_out, or_86_out);
  and and_293 (and_293_out, xor_79_out, or_87_out);
  xor xor_87 (xor_87_out, xor_79_out, or_87_out);
  and and_294 (and_294_out, xor_80_out, notconnected_12_out);
  xor xor_88 (xor_88_out, xor_80_out, notconnected_12_out);
  and and_295 (and_295_out, nor_25_out, dipswitch_8_out);
  nand nand_33 (nand_33_out, nand_36_out, nand_34_out);
  nand nand_34 (nand_34_out, nand_33_out, dipswitch_5_out);
  nand nand_35 (nand_35_out, nand_34_out, dipswitch_5_out, nand_36_out);
  nand nand_36 (nand_36_out, nand_35_out, NormalRegTest[7]);
  nand nand_37 (nand_37_out, nand_40_out, nand_38_out);
  nand nand_38 (nand_38_out, nand_37_out, dipswitch_5_out);
  nand nand_39 (nand_39_out, nand_38_out, dipswitch_5_out, nand_40_out);
  nand nand_40 (nand_40_out, nand_39_out, NormalRegTest[5]);
  nand nand_41 (nand_41_out, nand_44_out, nand_42_out);
  nand nand_42 (nand_42_out, nand_41_out, dipswitch_5_out);
  nand nand_43 (nand_43_out, nand_42_out, dipswitch_5_out, nand_44_out);
  nand nand_44 (nand_44_out, nand_43_out, NormalRegTest[3]);
  nand nand_45 (nand_45_out, nand_48_out, nand_46_out);
  nand nand_46 (nand_46_out, nand_45_out, dipswitch_5_out);
  nand nand_47 (nand_47_out, nand_46_out, dipswitch_5_out, nand_48_out);
  nand nand_48 (nand_48_out, nand_47_out, NormalRegTest[1]);
  nand nand_49 (nand_49_out, nand_34_out, nand_50_out);
  nand nand_50 (nand_50_out, nand_49_out, nand_35_out);
  nand nand_51 (nand_51_out, nand_38_out, nand_52_out);
  nand nand_52 (nand_52_out, nand_51_out, nand_39_out);
  nand nand_53 (nand_53_out, nand_42_out, nand_54_out);
  nand nand_54 (nand_54_out, nand_53_out, nand_43_out);
  nand nand_55 (nand_55_out, nand_46_out, nand_56_out);
  nand nand_56 (nand_56_out, nand_55_out, nand_47_out);
  assign driver_145_out = dipswitch_6_out ? nand_49_out : 1'bz;  // Driver driver_145
  assign driver_146_out = dipswitch_7_out ? nand_49_out : 1'bz;  // Driver driver_146
  assign driver_147_out = dipswitch_6_out ? nand_51_out : 1'bz;  // Driver driver_147
  assign driver_148_out = dipswitch_7_out ? nand_51_out : 1'bz;  // Driver driver_148
  assign driver_149_out = dipswitch_6_out ? nand_53_out : 1'bz;  // Driver driver_149
  assign driver_150_out = dipswitch_7_out ? nand_53_out : 1'bz;  // Driver driver_150
  assign driver_151_out = dipswitch_6_out ? nand_55_out : 1'bz;  // Driver driver_151
  assign driver_152_out = dipswitch_7_out ? nand_55_out : 1'bz;  // Driver driver_152
  // NotConnected on notconnected_13_out
  // NotConnected on notconnected_14_out
  // NotConnected on notconnected_15_out
  // NotConnected on notconnected_16_out
  and and_296 (and_296_out, notconnected_14_out[0], notconnected_14_out[0]);
  or or_88 (or_88_out, notconnected_15_out[0], notconnected_15_out[0]);
  xor xor_89 (xor_89_out, notconnected_16_out[0], notconnected_16_out[0]);
  and and_297 (and_297_out, notconnected_14_out[1], notconnected_14_out[1]);
  or or_89 (or_89_out, notconnected_15_out[1], notconnected_15_out[1]);
  xor xor_90 (xor_90_out, notconnected_16_out[1], notconnected_16_out[1]);
  not not_61 (not_61_out, notconnected_17_out);
  // NotConnected on notconnected_17_out
  and and_298 (and_298_out, notconnected_14_out[2], notconnected_14_out[2]);
  and and_299 (and_299_out, notconnected_14_out[3], notconnected_14_out[3]);
  or or_90 (or_90_out, notconnected_15_out[2], notconnected_15_out[2]);
  or or_91 (or_91_out, notconnected_15_out[3], notconnected_15_out[3]);
  xor xor_91 (xor_91_out, notconnected_16_out[2], notconnected_16_out[2]);
  xor xor_92 (xor_92_out, notconnected_16_out[3], notconnected_16_out[3]);
  // And and_300 has open pins: In_1=and_301_out, In_2=notconnected_13_out[7], out=open
  xor xor_93 (xor_93_out, notconnected_13_out[7], and_301_out);
  and and_301 (and_301_out, and_302_out, notconnected_13_out[6]);
  xor xor_94 (xor_94_out, notconnected_13_out[6], and_302_out);
  and and_302 (and_302_out, and_303_out, notconnected_13_out[5]);
  xor xor_95 (xor_95_out, notconnected_13_out[5], and_303_out);
  and and_303 (and_303_out, and_304_out, notconnected_13_out[4]);
  xor xor_96 (xor_96_out, notconnected_13_out[4], and_304_out);
  and and_304 (and_304_out, and_305_out, notconnected_13_out[3]);
  xor xor_97 (xor_97_out, notconnected_13_out[3], and_305_out);
  and and_305 (and_305_out, and_306_out, notconnected_13_out[2]);
  xor xor_98 (xor_98_out, notconnected_13_out[2], and_306_out);
  and and_306 (and_306_out, and_307_out, notconnected_13_out[1]);
  xor xor_99 (xor_99_out, notconnected_13_out[1], and_307_out);
  and and_307 (and_307_out, not_61_out, notconnected_13_out[0]);
  xor xor_100 (xor_100_out, notconnected_13_out[0], not_61_out);
  and and_308 (and_308_out, notconnected_14_out[4], notconnected_14_out[4]);
  or or_92 (or_92_out, notconnected_15_out[4], notconnected_15_out[4]);
  xor xor_101 (xor_101_out, notconnected_16_out[4], notconnected_16_out[4]);
  and and_309 (and_309_out, notconnected_14_out[5], notconnected_14_out[5]);
  or or_93 (or_93_out, notconnected_15_out[5], notconnected_15_out[5]);
  xor xor_102 (xor_102_out, notconnected_16_out[5], notconnected_16_out[5]);
  and and_310 (and_310_out, notconnected_14_out[6], notconnected_14_out[6]);
  and and_311 (and_311_out, notconnected_14_out[7], notconnected_14_out[7]);
  or or_94 (or_94_out, notconnected_15_out[6], notconnected_15_out[6]);
  or or_95 (or_95_out, notconnected_15_out[7], notconnected_15_out[7]);
  xor xor_103 (xor_103_out, notconnected_16_out[6], notconnected_16_out[6]);
  xor xor_104 (xor_104_out, notconnected_16_out[7], notconnected_16_out[7]);
  // NotConnected on notconnected_18_out
  // NotConnected on notconnected_19_out
  // NotConnected on notconnected_20_out
  // NotConnected on notconnected_21_out
  // NotConnected on notconnected_22_out
  // NotConnected on notconnected_23_out
  Button button_1 (.out(button_1_out));
  DipSwitch dipswitch_11 (.out(dipswitch_11_out));
  DipSwitch dipswitch_12 (.out(dipswitch_12_out));
  Reset #(.invertOutput("false")) reset_21 (.out(reset_21_out));
  and and_312 (and_312_out, notconnected_24_out, notconnected_18_out[0]);
  nand nand_57 (nand_57_out, notconnected_19_out[0], notconnected_19_out[0]);
  nor nor_27 (nor_27_out, notconnected_20_out[0], notconnected_20_out[0]);
  not not_62 (not_62_out, notconnected_23_out);
  CLA_Adder cla_adder_1 (.B(8'h1), .A(8'h1), .SUB(1'b1));  // open: OUT
  and and_313 (and_313_out, notconnected_24_out, notconnected_18_out[1]);
  and and_314 (and_314_out, notconnected_24_out, notconnected_18_out[2]);
  nand nand_58 (nand_58_out, notconnected_19_out[1], notconnected_19_out[1]);
  nand nand_59 (nand_59_out, notconnected_19_out[2], notconnected_19_out[2]);
  nor nor_28 (nor_28_out, notconnected_20_out[1], notconnected_20_out[1]);
  nor nor_29 (nor_29_out, notconnected_20_out[2], notconnected_20_out[2]);
  not not_63 (not_63_out, notconnected_22_out);
  not not_64 (not_64_out, notconnected_21_out);
  not not_65 (not_65_out, notconnected_23_out);
  not not_66 (not_66_out, notconnected_22_out);
  not not_67 (not_67_out, notconnected_21_out);
  not not_68 (not_68_out, not_62_out);
  // NotConnected on notconnected_24_out
  and and_315 (and_315_out, notconnected_24_out, notconnected_18_out[3]);
  nand nand_60 (nand_60_out, notconnected_19_out[3], notconnected_19_out[3]);
  nor nor_30 (nor_30_out, notconnected_20_out[3], notconnected_20_out[3]);
  and and_316 (and_316_out, not_64_out, not_63_out);
  and and_317 (and_317_out, notconnected_21_out, not_63_out);
  and and_318 (and_318_out, not_64_out, notconnected_22_out);
  and and_319 (and_319_out, notconnected_22_out, notconnected_21_out);
  and and_320 (and_320_out, not_67_out, not_66_out);
  and and_321 (and_321_out, notconnected_21_out, not_66_out);
  and and_322 (and_322_out, not_67_out, notconnected_22_out);
  and and_323 (and_323_out, notconnected_22_out, notconnected_21_out);
  _74TypeFlipFlop _74typeflipflop_74 (
    .CLK(button_1_out), .Data(TestAdvRegister[7]), .Load_A(dipswitch_11_out), .Load_B(dipswitch_12_out),
    .Always(TAR_always[7]), .Loaded_A(TAR_loadA[7]), .Loaded_B(TAR_loadB[7]), .Reset(reset_21_out));
  _74TypeFlipFlop _74typeflipflop_75 (
    .CLK(button_1_out), .Data(TestAdvRegister[6]), .Load_A(dipswitch_11_out), .Load_B(dipswitch_12_out),
    .Always(TAR_always[6]), .Loaded_A(TAR_loadA[6]), .Loaded_B(TAR_loadB[6]), .Reset(reset_21_out));
  _74TypeFlipFlop _74typeflipflop_76 (
    .CLK(button_1_out), .Data(TestAdvRegister[5]), .Load_A(dipswitch_11_out), .Load_B(dipswitch_12_out),
    .Always(TAR_always[5]), .Loaded_A(TAR_loadA[5]), .Loaded_B(TAR_loadB[5]), .Reset(reset_21_out));
  _74TypeFlipFlop _74typeflipflop_77 (
    .CLK(button_1_out), .Data(TestAdvRegister[4]), .Load_A(dipswitch_11_out), .Load_B(dipswitch_12_out),
    .Always(TAR_always[4]), .Loaded_A(TAR_loadA[4]), .Loaded_B(TAR_loadB[4]), .Reset(reset_21_out));
  _74TypeFlipFlop _74typeflipflop_78 (
    .CLK(button_1_out), .Data(TestAdvRegister[3]), .Load_A(dipswitch_11_out), .Load_B(dipswitch_12_out),
    .Always(TAR_always[3]), .Loaded_A(TAR_loadA[3]), .Loaded_B(TAR_loadB[3]), .Reset(reset_21_out));
  _74TypeFlipFlop _74typeflipflop_79 (
    .CLK(button_1_out), .Data(TestAdvRegister[2]), .Load_A(dipswitch_11_out), .Load_B(dipswitch_12_out),
    .Always(TAR_always[2]), .Loaded_A(TAR_loadA[2]), .Loaded_B(TAR_loadB[2]), .Reset(reset_21_out));
  _74TypeFlipFlop _74typeflipflop_80 (
    .CLK(button_1_out), .Data(TestAdvRegister[1]), .Load_A(dipswitch_11_out), .Load_B(dipswitch_12_out),
    .Always(TAR_always[1]), .Loaded_A(TAR_loadA[1]), .Loaded_B(TAR_loadB[1]), .Reset(reset_21_out));
  _74TypeFlipFlop _74typeflipflop_81 (
    .CLK(button_1_out), .Data(TestAdvRegister[0]), .Load_A(dipswitch_11_out), .Load_B(dipswitch_12_out),
    .Always(TAR_always[0]), .Loaded_A(TAR_loadA[0]), .Loaded_B(TAR_loadB[0]), .Reset(reset_21_out));
  ALUnoCLA alunocla_1 (.C_0(1'b1), .C_1(1'b1), .C_2(1'b1), .A_0(8'h1), .B_0(8'h1));  // open: C_Arith
  and and_324 (and_324_out, notconnected_24_out, notconnected_18_out[4]);
  nand nand_61 (nand_61_out, notconnected_19_out[4], notconnected_19_out[4]);
  nor nor_31 (nor_31_out, notconnected_20_out[4], notconnected_20_out[4]);
  and and_325 (and_325_out, and_316_out, not_65_out);
  and and_326 (and_326_out, and_317_out, not_65_out);
  and and_327 (and_327_out, and_318_out, not_65_out);
  and and_328 (and_328_out, and_319_out, not_65_out);
  and and_329 (and_329_out, and_320_out, not_68_out);
  and and_330 (and_330_out, and_321_out, not_68_out);
  and and_331 (and_331_out, and_322_out, not_68_out);
  and and_332 (and_332_out, and_323_out, not_68_out);
  and and_333 (and_333_out, notconnected_24_out, notconnected_18_out[5]);
  and and_334 (and_334_out, notconnected_24_out, notconnected_18_out[6]);
  nand nand_62 (nand_62_out, notconnected_19_out[5], notconnected_19_out[5]);
  nand nand_63 (nand_63_out, notconnected_19_out[6], notconnected_19_out[6]);
  nor nor_32 (nor_32_out, notconnected_20_out[5], notconnected_20_out[5]);
  nor nor_33 (nor_33_out, notconnected_20_out[6], notconnected_20_out[6]);
  and and_335 (and_335_out, notconnected_24_out, notconnected_18_out[7]);
  nand nand_64 (nand_64_out, notconnected_19_out[7], notconnected_19_out[7]);
  nor nor_34 (nor_34_out, notconnected_20_out[7], notconnected_20_out[7]);
  // NotConnected on notconnected_25_out
  assign driver_153_out = notconnected_26_out ? notconnected_25_out[0] : 1'bz;  // Driver driver_153
  assign driver_154_out = notconnected_26_out ? notconnected_25_out[1] : 1'bz;  // Driver driver_154
  assign driver_155_out = notconnected_26_out ? notconnected_25_out[2] : 1'bz;  // Driver driver_155
  assign driver_156_out = notconnected_26_out ? notconnected_25_out[3] : 1'bz;  // Driver driver_156
  assign driver_157_out = notconnected_26_out ? notconnected_25_out[4] : 1'bz;  // Driver driver_157
  assign driver_158_out = notconnected_26_out ? notconnected_25_out[5] : 1'bz;  // Driver driver_158
  assign driver_159_out = notconnected_26_out ? notconnected_25_out[6] : 1'bz;  // Driver driver_159
  // NotConnected on notconnected_26_out
  assign driver_160_out = notconnected_26_out ? notconnected_25_out[7] : 1'bz;  // Driver driver_160

  assign ARG1_2 = ARG1;
  assign ARG2_2 = ARG2;
  assign OPCODE_read = {OPCODE, ARG1, ARG2, DESTINATION};

  // Notes on the sheet:
  //   Z SWITCH
  //   Overwrite Value
  //   Overwrite
  //   Step
  //   COUNTER
  //   B
  //   Select
  //   MUX
  //   A
  //   .
  //   Register Saving
  //   Data
  //   Clock
  //   Load_A
  //   Load_B
  //   Reset
  //   SaveValue
  //   SaveLocation
  //   D flop with Pre and Res
  //   Preset
  //   Data Hazard Bypass
  //   OP_1 HAZARD
  //   Destination Disable
  //   XOR
  //   Last Tick Disabled
  //   OP_2 HAZARD
  //   Always
  //   Loaded_A
  //   Loaded_B
  //   OP_1 Immediate
  //   OP_2 Immediate
  //   DESTINATION sel
  //   Disable
  //   contents of Program_Memory (hex, n*v repeats v):
  //   80010000,a60000c0
  //   A_1
  //   A_0
  //   2x4 Demux
  //   Operation Decode
  //   000
  //   001
  //   010
  //   011
  //   100
  //   101
  //   110
  //   111
  //   OUTPUT
  //   Arithmetic
  //   Add
  //   Sub
  //   AND
  //   NAND
  //   OR
  //   NOR
  //   Unused
  //   A3
  //   Immediate Arg 1
  //   Immediate Arg 2
  //   Arithmetic/Compare
  //   RAM
  //   Argument
  //   Comparator
  //   EQUAL
  //   NEQ
  //   More
  //   Less
  //   MoreOrEqual
  //   LessOrEqual
  //   A1
  //   A2
  //   Arguments
  //   3x8 Demux
  //   ARG2 sel
  //   Many components are designed to
  //   take OPCODEs in and only use the
  //   last 3 argument bits.
  //   Compare
  //   Ram
  //   Main OPCODE Line
  //   Replace delay with system that saves values on the next tick. A register will hold the to save register and value. Then, it will save on that +1 tick to a register, ensuring it arrives before the clock. Selected operands should check if that register is about to be updated, and if so take the new data instead of old.
  //   Argument is another term for Operand
  //   Delay to make sure CLK signal does not arrive before Data is updated, otherwwise registers will never save. Update according to slowest result bus path that involves registers.
  //   ARG1 sel
  //   Immediates
  //   ARG2
  //   Immediate 2 Enable
  //   ARG1
  //   Immediate 1 Enable
  //   Immediate's Disable the corresponding argument sel
  //   Register 0
  //   Register 1
  //   Register 2
  //   Register 3
  //   Register 4
  //   Register 5
  //   Input
  //   SUBBER
  //   ALU
  //   ADDER/SUBBER
  //   Generate
  //   Propogate
  //   P_3
  //   G_3
  //   P_2
  //   G_2
  //   P_1
  //   G_1
  //   P_0
  //   G_0
  //   C_0
  //   4-bit Carry Look-ahead
  //   5Inp
  //   4Inp
  //   3Inp
  //   C_1
  //   C_4
  //   C_3
  //   C_2
  //   0's Conditional Unit
  //   Is less than 0 Unit
  //   Is!0 Unit
  //   Is0
  //   IsNot0
  //   Never
  //   COMPONENTS
  //   Register - outdated
  //   Edge Register
  //   Save
  //   Load
  //   Save Value
  //   Clk
  //   Load A
  //   Load B
  //   ADDER
  //   D
  //   Edge Flop
  //   Latch
  //   1 Bit mem
  //   SaveVal
  //   Write
  //   Loaded
  //   Always OUT
  //   OUT
  //   Always On Out
  //   Out
  //   INCRMNT
  //   Advanced Edge Register
  //   SWITCH FAKE
endmodule

/* Test case:
C_2 C_1 C_0 A_0 B_0 C_Arith
0 0 0 9 6 15 #addition and subtraction
0 0 1 9 6 3
0 0 0 6 7 13
0 0 1 111 67 44
0 0 0 32 59 91
0 1 0 51 60 48  #and
0 1 0 3 2 2
0 1 0 5 3 1
0 1 0 12 25 8
0 1 0 4 8 0
1 0 0 5 3 7 #or
1 0 0 2 8 10
1 0 0 12 25 29
1 0 0 0 7 7
0 1 1 1 1 254 #nand
0 1 1 2 4 255
0 1 1 15 3 252
1 0 1 1 0 254 #nor
1 0 1 3 5 248
1 0 1 128 64 63
1 1 0 5 3 6 #xor
1 1 0 10 10 0
1 1 0 85 170 255
1 1 0 14 1 15
*/

/* Test case:
In_3 In_2 In_1 Num_1 Out_0
0 0 0 4 0
0 0 1 5 1
0 0 0 210 0
0 0 1 253 1
0 1 1 65 0
0 1 0 102 1
0 1 1 237 1
0 1 0 179 0
1 0 0 102 1
1 0 0 0 1
1 0 0 252 0
1 0 1 179 1
1 0 1 0 1
1 0 1 112 0
1 1 0 0 1
1 1 0 243 1
1 1 0 123 1
1 1 1 0 0
1 1 1 243 0
1 1 1 123 0
*/

/* Test case:
D C L ALWAYS LOADED
# 1. Randomized Startup: Register state is unknown (X). LOADED is 0 because L=0.
0x00 0 0 X 0x00

# 2. Load 0xAA: ALWAYS updates to 0xAA. LOADED shows it because L=1.
0xAA C 1 0xAA 0xAA

# 3. Transparent Check: ALWAYS stays 0xAA. LOADED drops to 0x00 because L=0.
0x55 0 0 0xAA 0x00
0x21 C 0 0x21 0x00

# 5. Load 0x00: Register becomes 0. Both pins show 0.
0x00 C 1 0x00 0x00

# 6. Edge-Triggering: Data 0xEE only moves to ALWAYS on the rising edge.
0xEE 0 1 0x00 0x00  # L=1, but no clock yet; LOADED is 0 because reg is 0
0xEE 1 1 0xEE 0xEE  # Clock goes high; Reg becomes 0xEE. LOADED now shows it.
0xDD 0 1 0xEE 0xEE  # Clock falls; Reg stays 0xEE.

# 7. High-Clock Stability Test
0xAA 0 1 0xEE 0xEE  # Prepare data 0xAA, but clock is 0. ALWAYS stays 0xEE.
0xAA 1 1 0xAA 0xAA  # Clock goes High. Register captures 0xAA.
0xFF 1 1 0xAA 0xAA  # DATA CHANGES TO 0xFF WHILE CLOCK IS STILL HIGH.
                    # ALWAYS MUST STAY 0xAA. If it changes to 0xFF, it's a latch!
*/
